// Logisim project CPU (2).circ as structural Verilog: 12 circuits, main circuit 138
module RAM_Board (
  input  [7:0] nDL,
  input  [7:0] nDH,
  input  [7:0] nAL,
  input  [7:0] nAH
);
endmodule

module _138 (
  input  a,
  input  b,
  input  c,
  input  g1,
  input  ng2a,
  input  ng2b,
  output ny0,
  output ny1,
  output ny2,
  output ny3,
  output ny4,
  output ny5,
  output ny6,
  output ny7
);

  wire and_1_out;

  and and_1 (and_1_out, g1, ~ng2a, ~ng2b);  // AND_Gate
  nand nand_1 (ny0, ~a, ~b, ~c, and_1_out);  // NAND_Gate
  nand nand_2 (ny1, a, ~b, ~c, and_1_out);  // NAND_Gate
  nand nand_3 (ny2, ~a, b, ~c, and_1_out);  // NAND_Gate
  nand nand_4 (ny3, a, b, ~c, and_1_out);  // NAND_Gate
  nand nand_5 (ny4, ~a, ~b, c, and_1_out);  // NAND_Gate
  nand nand_6 (ny5, a, ~b, c, and_1_out);  // NAND_Gate
  nand nand_7 (ny6, ~a, b, c, and_1_out);  // NAND_Gate
  nand nand_8 (ny7, a, b, c, and_1_out);
endmodule

module _151 (
  input  a,
  input  b,
  input  c,
  input  ng,
  input  d0,
  input  d1,
  input  d2,
  input  d3,
  input  d4,
  input  d5,
  input  d6,
  input  d7,
  output y,
  output ny
);

  wire and_1_out, and_2_out, and_3_out, and_4_out, and_5_out, and_6_out, and_7_out, and_8_out;

  and and_1 (and_1_out, d0, ~a, ~b, ~c, ~ng);  // AND_Gate
  and and_2 (and_2_out, d1, a, ~b, ~c, ~ng);  // AND_Gate
  and and_3 (and_3_out, d2, ~a, b, ~c, ~ng);  // AND_Gate
  and and_4 (and_4_out, d3, a, b, ~c, ~ng);  // AND_Gate
  and and_5 (and_5_out, d4, ~a, ~b, c, ~ng);  // AND_Gate
  and and_6 (and_6_out, d5, a, ~b, c, ~ng);  // AND_Gate
  and and_7 (and_7_out, d6, ~a, b, c, ~ng);  // AND_Gate
  and and_8 (and_8_out, d7, a, b, c, ~ng);  // AND_Gate
  or or_1 (y, and_1_out, and_2_out, and_3_out, and_4_out, and_5_out, and_6_out, and_7_out, and_8_out);
  not not_1 (ny, y);
endmodule

module _153 (
  input  a,
  input  b,
  input  _1g,
  input  _1c0,
  input  _1c1,
  input  _1c2,
  input  _1c3,
  input  _2g,
  input  _2c0,
  input  _2c1,
  input  _2c2,
  input  _2c3,
  output _1y,
  output _2y
);

  wire and_1_out, and_2_out, and_3_out, and_4_out, and_5_out, and_6_out, and_7_out, and_8_out;

  and and_1 (and_1_out, ~_1g, ~a, ~b, _1c0);  // AND_Gate
  and and_2 (and_2_out, ~_1g, a, ~b, _1c1);  // AND_Gate
  and and_3 (and_3_out, ~_1g, ~a, b, _1c2);  // AND_Gate
  and and_4 (and_4_out, ~_1g, a, b, _1c3);  // AND_Gate
  and and_5 (and_5_out, ~_2g, ~a, ~b, _2c0);  // AND_Gate
  and and_6 (and_6_out, ~_2g, a, ~b, _2c1);  // AND_Gate
  and and_7 (and_7_out, ~_2g, ~a, b, _2c2);  // AND_Gate
  and and_8 (and_8_out, ~_2g, a, b, _2c3);  // AND_Gate
  or or_1 (_1y, and_1_out, and_2_out, and_3_out, and_4_out);
  or or_2 (_2y, and_5_out, and_6_out, and_7_out, and_8_out);
endmodule

module _169 (
  input  [3:0] P,
  input  clk,
  input  npe,
  input  u_d,
  input  ncet,
  input  ncep,
  output ntc,
  output [3:0] Q
);

  wire and_1_out, and_2_out, and_3_out, and_4_out, and_5_out, and_6_out, and_7_out, and_8_out, and_9_out,
       and_10_out, and_11_out, and_12_out, and_13_out, and_14_out, and_15_out, and_16_out, and_17_out,
       and_18_out, and_19_out, and_20_out, and_21_out, or_1_out, or_2_out, or_3_out, or_4_out, or_5_out,
       or_6_out, or_7_out, or_8_out, or_9_out, or_10_out;

  and and_1 (and_1_out, ~ncet, ~ncep);  // AND_Gate
  and and_2 (and_2_out, ~npe, P[0]);  // AND_Gate
  and and_3 (and_3_out, ~Q[0], and_1_out, npe);  // AND_Gate
  or or_1 (or_1_out, and_3_out, and_2_out, and_4_out);
  and and_4 (and_4_out, Q[0], ~and_1_out, npe);  // AND_Gate
  and and_5 (and_5_out, Q[0], ~Q[1], and_1_out, u_d, npe);  // AND_Gate
  D_Flip_Flop d_ff_1 (.clk(clk), .D(or_1_out), .Q(Q[0]));  // open: Qn, preset, en, reset
  and and_6 (and_6_out, ~npe, P[1]);  // AND_Gate
  or or_2 (or_2_out, ~and_1_out, ~Q[0]);  // OR_Gate
  and and_7 (and_7_out, or_2_out, Q[1], u_d, npe);
  or or_3 (or_3_out, and_5_out, and_7_out, and_6_out, and_8_out, and_10_out);
  or or_4 (or_4_out, ~and_1_out, Q[0]);  // OR_Gate
  and and_8 (and_8_out, ~Q[0], ~Q[1], and_1_out, ~u_d, npe);  // AND_Gate
  D_Flip_Flop d_ff_2 (.clk(clk), .D(or_3_out), .Q(Q[1]));  // open: Qn, preset, en, reset
  and and_9 (and_9_out, Q[0], Q[1], ~Q[2], and_1_out, u_d, npe);  // AND_Gate
  and and_10 (and_10_out, or_4_out, Q[1], ~u_d, npe);  // AND_Gate
  or or_5 (or_5_out, ~and_1_out, ~Q[0], ~Q[1]);  // OR_Gate
  and and_11 (and_11_out, or_5_out, Q[2], u_d, npe);
  and and_12 (and_12_out, ~npe, P[2]);  // AND_Gate
  and and_13 (and_13_out, ~Q[0], ~Q[1], ~Q[2], and_1_out, ~u_d, npe);  // AND_Gate
  or or_6 (or_6_out, and_9_out, and_11_out, and_12_out, and_13_out, and_14_out);
  D_Flip_Flop d_ff_3 (.clk(clk), .D(or_6_out), .Q(Q[2]));  // open: Qn, preset, en, reset
  or or_7 (or_7_out, ~and_1_out, Q[0], Q[1]);  // OR_Gate
  and and_14 (and_14_out, or_7_out, Q[2], ~u_d, npe);  // AND_Gate
  or or_8 (or_8_out, ~and_1_out, ~Q[0], ~Q[1], ~Q[2]);  // OR_Gate
  and and_15 (and_15_out, Q[0], Q[1], Q[2], ~Q[3], and_1_out, u_d, npe);  // AND_Gate
  and and_16 (and_16_out, ~npe, P[3]);  // AND_Gate
  and and_17 (and_17_out, or_8_out, Q[3], u_d, npe);
  or or_9 (or_9_out, and_15_out, and_17_out, and_16_out, and_18_out, and_19_out);
  or or_10 (or_10_out, ~and_1_out, Q[0], Q[1], Q[2]);  // OR_Gate
  and and_18 (and_18_out, ~Q[0], ~Q[1], ~Q[2], ~Q[3], and_1_out, ~u_d, npe);  // AND_Gate
  D_Flip_Flop d_ff_4 (.clk(clk), .D(or_9_out), .Q(Q[3]));  // open: Qn, preset, en, reset
  and and_19 (and_19_out, or_10_out, Q[3], ~u_d, npe);  // AND_Gate
  and and_20 (and_20_out, u_d, ~ncet, Q[0], Q[1], Q[2], Q[3]);  // AND_Gate
  and and_21 (and_21_out, ~u_d, ~ncet, ~Q[0], ~Q[1], ~Q[2], ~Q[3]);  // AND_Gate
  nor nor_1 (ntc, and_20_out, and_21_out);
endmodule

module _181 (
  input  [3:0] nA,
  input  [3:0] nB,
  input  [3:0] S,
  input  m,
  input  cn,
  output cn_4,
  output zero,
  output ng,
  output np,
  output [3:0] nF
);

  wire and_1_out, and_2_out, and_3_out, and_4_out, and_5_out, and_6_out, and_7_out, and_8_out, and_9_out,
       and_10_out, and_11_out, and_12_out, and_13_out, and_14_out, and_15_out, and_16_out, and_17_out,
       and_18_out, and_19_out, and_20_out, and_21_out, and_22_out, and_23_out, and_24_out, and_26_out,
       and_27_out, and_28_out, and_29_out, nand_1_out, nand_3_out, nor_1_out, nor_2_out, nor_3_out,
       nor_4_out, nor_5_out, nor_6_out, nor_7_out, nor_8_out, nor_9_out, nor_10_out, nor_11_out, not_1_out,
       xor_2_out, xor_3_out, xor_5_out, xor_8_out;

  and and_1 (and_1_out, nB[0], S[0]);
  nor nor_1 (nor_1_out, nA[0], and_1_out, and_3_out);
  not not_1 (not_1_out, m);
  nand nand_1 (nand_1_out, cn, not_1_out);
  xor xor_1 (nF[0], nand_1_out, xor_2_out);
  and and_2 (and_2_out, nA[0], ~nB[0], S[2]);  // AND_Gate
  and and_3 (and_3_out, ~nB[0], S[1]);  // AND_Gate
  and and_4 (and_4_out, cn, nor_4_out, not_1_out);
  and and_5 (and_5_out, nor_1_out, not_1_out);
  nor nor_2 (nor_2_out, and_5_out, and_4_out);
  xor xor_2 (xor_2_out, nor_1_out, nor_4_out);
  and and_6 (and_6_out, nB[1], S[0]);
  and and_7 (and_7_out, nA[0], nB[0], S[3]);
  nor nor_3 (nor_3_out, nA[1], and_6_out, and_10_out);
  nor nor_4 (nor_4_out, and_2_out, and_7_out);
  and and_8 (and_8_out, nor_3_out, not_1_out);
  xor xor_3 (xor_3_out, nor_3_out, nor_7_out);
  xor xor_4 (nF[1], nor_2_out, xor_3_out);
  and and_9 (and_9_out, nA[1], ~nB[1], S[2]);  // AND_Gate
  and and_10 (and_10_out, ~nB[1], S[1]);  // AND_Gate
  and and_11 (and_11_out, cn, nor_4_out, nor_7_out, not_1_out);
  and and_12 (and_12_out, nor_1_out, nor_7_out, not_1_out);
  nor nor_5 (nor_5_out, and_8_out, and_12_out, and_11_out);
  and and_13 (and_13_out, nA[1], nB[1], S[3]);
  and and_14 (and_14_out, nB[2], S[0]);
  nor nor_6 (nor_6_out, nA[2], and_14_out, and_17_out);
  nor nor_7 (nor_7_out, and_9_out, and_13_out);
  and and_15 (and_15_out, nor_6_out, not_1_out);
  xor xor_5 (xor_5_out, nor_6_out, nor_9_out);
  xor xor_6 (nF[2], nor_5_out, xor_5_out);
  and and_16 (and_16_out, nA[2], ~nB[2], S[2]);  // AND_Gate
  and and_17 (and_17_out, ~nB[2], S[1]);  // AND_Gate
  and and_18 (and_18_out, nor_1_out, nor_7_out, nor_9_out, not_1_out);
  and and_19 (and_19_out, nor_3_out, nor_9_out, not_1_out);
  nor nor_8 (nor_8_out, and_15_out, and_19_out, and_18_out, and_22_out);
  and and_20 (and_20_out, nA[2], nB[2], S[3]);
  and and_21 (and_21_out, nB[3], S[0]);
  nor nor_9 (nor_9_out, and_16_out, and_20_out);
  nor nor_10 (nor_10_out, nA[3], and_21_out, and_23_out);
  and and_22 (and_22_out, cn, nor_4_out, nor_7_out, nor_9_out, not_1_out);
  xor xor_7 (nF[3], nor_8_out, xor_8_out);
  and and_23 (and_23_out, ~nB[3], S[1]);  // AND_Gate
  and and_24 (and_24_out, nA[3], ~nB[3], S[2]);  // AND_Gate
  nand nand_2 (np, nor_4_out, nor_7_out, nor_9_out, nor_11_out);
  xor xor_8 (xor_8_out, nor_10_out, nor_11_out);
  and and_25 (zero, nF[0], nF[1], nF[2], nF[3]);
  and and_26 (and_26_out, nA[3], nB[3], S[3]);
  nor nor_11 (nor_11_out, and_24_out, and_26_out);
  nand nand_3 (nand_3_out, cn, nor_4_out, nor_7_out, nor_9_out, nor_11_out);
  and and_27 (and_27_out, nor_3_out, nor_9_out, nor_11_out);
  and and_28 (and_28_out, nor_1_out, nor_7_out, nor_9_out, nor_11_out);
  nor nor_12 (ng, and_28_out, and_27_out, and_29_out, nor_10_out);
  and and_29 (and_29_out, nor_6_out, nor_11_out);
  or or_1 (cn_4, ~nand_3_out, ~ng);  // OR_Gate

  // Notes on the sheet:
  //   and_25 drives only 0 and floats otherwise
endmodule

module _182 (
  input  ng0,
  input  np0,
  input  ng1,
  input  np1,
  input  ng2,
  input  np2,
  input  ng3,
  input  np3,
  input  cn,
  output cn_x,
  output cn_y,
  output cn_z,
  output ng,
  output np
);

  wire and_1_out, and_2_out, and_3_out, and_4_out, and_5_out, and_6_out, and_7_out, and_8_out, and_9_out,
       and_10_out, and_11_out, and_12_out, and_13_out, not_1_out;

  not not_1 (not_1_out, cn);
  and and_1 (and_1_out, ng0, not_1_out);
  and and_2 (and_2_out, ng0, np0);
  nor nor_1 (cn_x, and_2_out, and_1_out);
  and and_3 (and_3_out, ng1, np1);
  and and_4 (and_4_out, ng0, np0, ng1);
  nor nor_2 (cn_y, and_3_out, and_4_out, and_5_out);
  and and_5 (and_5_out, ng0, ng1, not_1_out);
  and and_6 (and_6_out, ng2, np2);
  and and_7 (and_7_out, ng1, np1, ng2);
  nor nor_3 (cn_z, and_6_out, and_7_out, and_8_out, and_10_out);
  and and_8 (and_8_out, ng0, np0, ng1, ng2);
  and and_9 (and_9_out, ng3, np3);
  and and_10 (and_10_out, ng0, ng1, ng2, not_1_out);
  and and_11 (and_11_out, ng2, np2, ng3);
  or or_1 (ng, and_9_out, and_11_out, and_13_out, and_12_out);
  and and_12 (and_12_out, ng0, ng1, ng2, ng3);
  and and_13 (and_13_out, ng1, np1, ng2, ng3);
  or or_2 (np, np0, np1, np2, np3);
endmodule

// 279
module _279_1 (
  input  nr,
  input  ns1,
  input  ns2,
  output q
);

  wire nand_1_out;

  nand nand_1 (nand_1_out, nr, q);
  nand nand_2 (q, nand_1_out, ns1, ns2);
endmodule

// 279
module _279_2 (
  input  nr,
  input  ns,
  output q
);

  wire nand_1_out;

  nand nand_1 (nand_1_out, nr, q);
  nand nand_2 (q, nand_1_out, ns);
endmodule

module _377 (
  input  [7:0] D,
  input  clk,
  input  ng,
  output [7:0] Q
);

  wire and_1_out, and_2_out;

  and and_1 (and_1_out, clk, ~and_2_out);  // AND_Gate
  and and_2 (and_2_out, ~and_1_out, ~ng);  // AND_Gate
  D_Flip_Flop d_ff_1 (.clk(clk), .D(D[0]), .Q(Q[0]), .en(and_2_out));  // open: Qn, preset, reset
  D_Flip_Flop d_ff_2 (.clk(clk), .D(D[1]), .Q(Q[1]), .en(and_2_out));  // open: Qn, preset, reset
  D_Flip_Flop d_ff_3 (.clk(clk), .D(D[2]), .Q(Q[2]), .en(and_2_out));  // open: Qn, preset, reset
  D_Flip_Flop d_ff_4 (.clk(clk), .D(D[3]), .Q(Q[3]), .en(and_2_out));  // open: Qn, preset, reset
  D_Flip_Flop d_ff_5 (.clk(clk), .D(D[4]), .Q(Q[4]), .en(and_2_out));  // open: Qn, preset, reset
  D_Flip_Flop d_ff_6 (.clk(clk), .D(D[5]), .Q(Q[5]), .en(and_2_out));  // open: Qn, preset, reset
  D_Flip_Flop d_ff_7 (.clk(clk), .D(D[6]), .Q(Q[6]), .en(and_2_out));  // open: Qn, preset, reset
  D_Flip_Flop d_ff_8 (.clk(clk), .D(D[7]), .Q(Q[7]), .en(and_2_out));  // open: Qn, preset, reset
endmodule

module _641 (
  input  [7:0] A,
  input  a_b,
  input  ng,
  input  [7:0] B,
  output [7:0] A_2,
  output [7:0] B_2
);

  wire and_1_out, and_2_out;

  and and_1 (and_1_out, a_b, ~ng);  // AND_Gate
  nand nand_1 (B_2[0], and_1_out, ~A[0]);  // NAND_Gate
  and and_2 (and_2_out, ~a_b, ~ng);  // AND_Gate
  nand nand_2 (A_2[0], and_2_out, ~B[0]);  // NAND_Gate
  nand nand_3 (B_2[1], and_1_out, ~A[1]);  // NAND_Gate
  nand nand_4 (A_2[1], and_2_out, ~B[1]);  // NAND_Gate
  nand nand_5 (B_2[2], and_1_out, ~A[2]);  // NAND_Gate
  nand nand_6 (A_2[2], and_2_out, ~B[2]);  // NAND_Gate
  nand nand_7 (B_2[3], and_1_out, ~A[3]);  // NAND_Gate
  nand nand_8 (A_2[3], and_2_out, ~B[3]);  // NAND_Gate
  nand nand_9 (B_2[4], and_1_out, ~A[4]);  // NAND_Gate
  nand nand_10 (A_2[4], and_2_out, ~B[4]);  // NAND_Gate
  nand nand_11 (B_2[5], and_1_out, ~A[5]);  // NAND_Gate
  nand nand_12 (A_2[5], and_2_out, ~B[5]);  // NAND_Gate
  nand nand_13 (B_2[6], and_1_out, ~A[6]);  // NAND_Gate
  nand nand_14 (A_2[6], and_2_out, ~B[6]);  // NAND_Gate
  nand nand_15 (B_2[7], and_1_out, ~A[7]);  // NAND_Gate
  nand nand_16 (A_2[7], and_2_out, ~B[7]);  // NAND_Gate

  // Notes on the sheet:
  //   nand_1 drives only 0 and floats otherwise
  //   nand_2 drives only 0 and floats otherwise
  //   nand_3 drives only 0 and floats otherwise
  //   nand_4 drives only 0 and floats otherwise
  //   nand_5 drives only 0 and floats otherwise
  //   nand_6 drives only 0 and floats otherwise
  //   nand_7 drives only 0 and floats otherwise
  //   nand_8 drives only 0 and floats otherwise
  //   nand_9 drives only 0 and floats otherwise
  //   nand_10 drives only 0 and floats otherwise
  //   nand_11 drives only 0 and floats otherwise
  //   nand_12 drives only 0 and floats otherwise
  //   nand_13 drives only 0 and floats otherwise
  //   nand_14 drives only 0 and floats otherwise
  //   nand_15 drives only 0 and floats otherwise
  //   nand_16 drives only 0 and floats otherwise
endmodule

module _62256 (
  input  [7:0] D,
  input  clk,
  input  ncs,
  input  noe,
  input  nwe,
  input  [14:0] A,
  output [7:0] D_2
);

  wire and_1_out, and_2_out, not_1_out;
  wire [7:0] controlled_buffer_1_out;

  and and_1 (and_1_out, ~ncs, ~noe, nwe);  // AND_Gate
  and and_2 (and_2_out, ~ncs, ~nwe);  // AND_Gate
  not not_1 (not_1_out, and_2_out);
  assign controlled_buffer_1_out = and_2_out ? D : 8'bz;  // Controlled_Buffer controlled_buffer_1
  RAM #(.addrWidth(15)) ram_1 (
    .addr(A), .data(controlled_buffer_1_out), .clk(clk), .ld(not_1_out), .clr(1'b0));  // open: sel
  assign D_2 = and_1_out ? controlled_buffer_1_out : 8'bz;  // Controlled_Buffer controlled_buffer_2
endmodule
