// Logisim project CPU-1.circ as structural Verilog: 19 circuits, main circuit CPU
module CPU (
  input  run,
  input  step,
  input  al,
  input  exam,
  input  dep,
  input  [15:0] S
);

  wire alu_board_1_c, alu_board_1_nn, alu_board_1_z, clock_1_out, control_board_1_nc, control_board_1_nn_2,
       control_board_1_nread, control_board_1_nwrite, control_board_1_nz, not_3_out, not_5_out, not_6_out,
       not_7_out, not_10_out, not_12_out, not_13_out, not_16_out, ram_decoder_board_1__0xxx,
       ram_decoder_board_1__1xxx;
  wire [6:0] control_board_1_nstate, not_11_out;
  wire [8:0] control_board_1_ncontrol;
  wire [15:0] alu_board_1_na, alu_board_1_nb, alu_board_1_nf, not_1_out, not_2_out, not_4_out, not_8_out,
       not_9_out, not_14_out, not_15_out, not_17_out, not_18_out, pull_resistor_1_node, pull_resistor_2_node,
       register_board_1_na, register_board_1_nd, register_board_1_np;

  Pull_Resistor #(.pull(1)) pull_resistor_1 (.node(pull_resistor_1_node));
  Clock clock_1 (.out(clock_1_out));
  assign not_1_out = ~pull_resistor_1_node;  // NOT_Gate not_1, 16 bits wide
  // Probe on not_1_out
  Pull_Resistor #(.pull(1)) pull_resistor_2 (.node(pull_resistor_2_node));
  assign not_2_out = ~pull_resistor_2_node;  // NOT_Gate not_2, 16 bits wide
  // Probe on not_2_out
  RAM_Decoder_Board ram_decoder_board_1 (
    ._0xxx(ram_decoder_board_1__0xxx), ._1xxx(ram_decoder_board_1__1xxx), .nData(pull_resistor_1_node),
    .nData_2(pull_resistor_1_node), .clk(clock_1_out), .nread(control_board_1_nread),
    .nwrite(control_board_1_nwrite), .nAddress(pull_resistor_2_node));  // open: _2xxx, _3xxx, _4xxx, _5xxx, _6xxx, _7xxx
  not not_3 (not_3_out, run);
  ALU_Board alu_board_1 (
    .clk(clock_1_out), .nread(control_board_1_nread), .nwrite(control_board_1_nwrite),
    .nData(pull_resistor_1_node), .nData_2(pull_resistor_1_node), .nAddress(pull_resistor_2_node),
    .nA(alu_board_1_na), .nB(alu_board_1_nb), .nF(alu_board_1_nf), .ng(ram_decoder_board_1__1xxx),
    .c(alu_board_1_c), .z(alu_board_1_z), .nn(alu_board_1_nn));
  assign not_4_out = ~alu_board_1_na;  // NOT_Gate not_4, 16 bits wide
  // Probe on not_4_out
  not not_5 (not_5_out, step);
  not not_6 (not_6_out, al);
  not not_7 (not_7_out, exam);
  assign not_8_out = ~alu_board_1_nb;  // NOT_Gate not_8, 16 bits wide
  assign not_9_out = ~alu_board_1_nf;  // NOT_Gate not_9, 16 bits wide
  // Probe on not_9_out
  // Probe on not_8_out
  not not_10 (not_10_out, dep);
  Control_Board control_board_1 (
    .clk(clock_1_out), .nrun(not_3_out), .nstep(not_5_out), .nal(not_6_out), .nexam(not_7_out),
    .ndep(not_10_out), .nControl(control_board_1_ncontrol), .nread(control_board_1_nread),
    .nwrite(control_board_1_nwrite), .nState(control_board_1_nstate), .ng(ram_decoder_board_1__0xxx),
    .nc(control_board_1_nc), .nz(control_board_1_nz), .nn_2(control_board_1_nn_2), .c(alu_board_1_c),
    .z(alu_board_1_z), .nn(alu_board_1_nn), .nAddress(pull_resistor_2_node));
  assign not_11_out = ~control_board_1_nstate;  // NOT_Gate not_11, 7 bits wide
  // Probe on not_11_out
  not not_12 (not_12_out, control_board_1_nz);
  not not_13 (not_13_out, control_board_1_nc);
  // Probe on not_12_out
  // Probe on not_13_out
  assign not_14_out = ~S;  // NOT_Gate not_14, 16 bits wide
  Register_Board register_board_1 (
    .clk(clock_1_out), .nS(not_14_out), .nD(register_board_1_nd), .nA(register_board_1_na),
    .nP(register_board_1_np), .nData(pull_resistor_1_node), .nData_2(pull_resistor_1_node),
    .nAddress(pull_resistor_2_node), .nControl(control_board_1_ncontrol));
  assign not_15_out = ~register_board_1_nd;  // NOT_Gate not_15, 16 bits wide
  not not_16 (not_16_out, control_board_1_nn_2);
  // Probe on not_16_out
  // Probe on not_15_out
  assign not_17_out = ~register_board_1_np;  // NOT_Gate not_17, 16 bits wide
  assign not_18_out = ~register_board_1_na;  // NOT_Gate not_18, 16 bits wide
  // Probe on not_17_out
  // Probe on not_18_out
endmodule

module Control_Board (
  input  clk,
  input  ng,
  input  nrun,
  input  nstep,
  input  nal,
  input  nexam,
  input  ndep,
  input  c,
  input  z,
  input  nn,
  input  [15:0] nAddress,
  output [8:0] nControl,
  output nc,
  output nz,
  output nn_2,
  output nread,
  output nwrite,
  output [6:0] nState
);

  wire _04_3_out, _11_out, _32_out, _40_out, n151_1_ny;
  wire [7:0] _32_5_out;
  wire [7:7] n377_1_q;

  not _04 (nc, c);
  not _04_2 (nz, z);
  not _04_3 (_04_3_out, nn);
  _151 u_151_1 (
    .a(nAddress[0]), .b(nAddress[1]), .c(nAddress[2]), .ng(ng), .d0(nn), .d1(_04_3_out), .d2(nz), .d3(z),
    .d4(nc), .d5(c), .d6(1'b0), .d7(1'b1), .ny(n151_1_ny));  // open: y
  _377 u_377_1 (
    .clk(clk), .ng(1'b0), .D({_32_5_out[7:4], nState[4], nState[5], nState[6], _32_5_out[0]}),
    .Q({n377_1_q[7], nState[0], nState[1], nState[2], nControl[2], nState[4], nState[5], nState[6]}));
  nand _40 (_40_out, 1'b1, nState[6], nState[5], nState[4]);
  and _11 (_11_out, 1'b1, nrun, _32_out);
  or _32 (_32_out, n377_1_q[7], nstep);
  or _32_2 (_32_5_out[4], n377_1_q[7], nal);
  or _32_3 (_32_5_out[5], n377_1_q[7], nexam);
  or _32_4 (_32_5_out[6], n377_1_q[7], ndep);
  nand _40_2 (_32_5_out[7], nstep, nal, nexam, ndep);
  and _21 (nread, nState[6], nState[5], nState[4], nState[1]);
  and _21_2 (nwrite, nControl[2], nState[0], 1'b1, 1'b1);
  or _32_5 (_32_5_out[0], _40_out, _11_out);
  and _08 (nControl[0], nState[2], nState[0]);
  and _08_2 (nControl[1], nState[5], nState[1]);
  and _11_2 (nControl[3], nState[6], nState[4], nState[2]);
  and _08_3 (nControl[4], nState[1], nState[0]);
  and _11_3 (nControl[5], nState[1], nState[5], nwrite);
  or _32_6 (nControl[6], nwrite, n151_1_ny);
  and _08_4 (nControl[7], nState[4], nState[6]);
  or _32_7 (nControl[8], n151_1_ny, nread);

  assign nn_2 = nn;
  assign nState[3] = nControl[2];
endmodule

// Reg Board
module Register_Board (
  input  [15:0] nData,
  input  clk,
  input  [15:0] nS,
  input  [8:0] nControl,
  output [15:0] nData_2,
  output [15:0] nD,
  output [15:0] nA,
  output [15:0] nP,
  output [15:0] nAddress
);

  OC_Buffer oc_buffer_1 (.ng(nControl[0]), .In(nS), .Out(nData_2));
  Register register_1 (.clk(clk), .Q(nD), .nwe(nControl[1]), .D(nData));
  OC_Buffer oc_buffer_2 (.ng(nControl[2]), .In(nD), .Out(nData_2));
  Counter counter_1 (.nwe(nControl[3]), .nce(nControl[4]), .u_d(1'b0), .clk(clk), .Q(nA), .P(nData));  // open: ntc
  OC_Buffer oc_buffer_3 (.ng(nControl[5]), .In(nA), .Out(nAddress));
  Counter counter_2 (.nwe(nControl[6]), .nce(nControl[7]), .u_d(1'b0), .clk(clk), .Q(nP), .P(nData));  // open: ntc
  OC_Buffer oc_buffer_4 (.ng(nControl[7]), .In(nP), .Out(nAddress));
  OC_Buffer oc_buffer_5 (.ng(nControl[8]), .In(nP), .Out(nData_2));
endmodule

// RAM&Decoder
module RAM_Decoder_Board (
  input  [15:0] nData,
  input  clk,
  input  nread,
  input  nwrite,
  input  [15:0] nAddress,
  output [15:0] nData_2,
  output _0xxx,
  output _1xxx,
  output _2xxx,
  output _3xxx,
  output _4xxx,
  output _5xxx,
  output _6xxx,
  output _7xxx
);

  wire n153_1__1y, n153_1__2y;
  wire [7:0] n62256_1_d_2, oc_transceiver_1_b_2;

  _62256 u_62256_1 (
    .clk(clk), .ncs(nAddress[15]), .nwe(nwrite), .noe(nread), .D(n62256_1_d_2), .D_2(n62256_1_d_2),
    .A(nAddress[14:0]));
  OC_Transceiver oc_transceiver_1 (
    .ng(n153_1__2y), .A(nData), .A_2(nData_2), .B_2({oc_transceiver_1_b_2, n62256_1_d_2}),
    .B({oc_transceiver_1_b_2, n62256_1_d_2}), .a_b(n153_1__1y));
  _153 u_153_1 (
    .a(nread), .b(nwrite), ._1g(1'b0), ._1c0(1'b1), ._1c1(1'b1), ._1c2(nAddress[15]), ._1c3(1'b1),
    ._2g(1'b0), ._2c0(nAddress[15]), ._2c1(nAddress[15]), ._2c2(nAddress[15]), ._2c3(1'b1), ._1y(n153_1__1y),
    ._2y(n153_1__2y));
  Pull_Resistor #(.pull(1)) pull_resistor_1 (.node({oc_transceiver_1_b_2, n62256_1_d_2}));
  _138 u_138_1 (
    .a(nAddress[12]), .b(nAddress[13]), .c(nAddress[14]), .g1(nAddress[15]), .ng2a(1'b0), .ng2b(1'b0),
    .ny0(_7xxx), .ny1(_6xxx), .ny2(_5xxx), .ny3(_4xxx), .ny4(_3xxx), .ny5(_2xxx), .ny6(_1xxx), .ny7(_0xxx));
  _62256 u_62256_2 (
    .clk(clk), .ncs(nAddress[15]), .nwe(nwrite), .noe(nread), .D(oc_transceiver_1_b_2),
    .D_2(oc_transceiver_1_b_2), .A(nAddress[14:0]));
endmodule

module ALU_Board (
  input  clk,
  input  ng,
  input  [15:0] nData,
  input  nread,
  input  nwrite,
  input  [15:0] nAddress,
  output [15:0] nData_2,
  output [15:0] nA,
  output [15:0] nB,
  output [15:0] nF,
  output c,
  output z,
  output nn
);

  wire _32_2_out, _32_3_out, _32_4_out, _32_out, n153_1__1y, n153_1__2y;
  wire [7:0] n377_1_q, n377_2_q;

  or _32 (_32_out, ng, nread);
  or _32_2 (_32_2_out, ng, nwrite);
  or _32_3 (_32_3_out, _32_2_out, nAddress[6]);
  or _32_4 (_32_4_out, _32_2_out, nAddress[7]);
  _377 u_377_1 (.clk(clk), .ng(_32_4_out), .D({{7{1'b0}}, c}), .Q(n377_1_q));
  _377 u_377_2 (.clk(clk), .ng(_32_2_out), .D({2'b00, nAddress[5:0]}), .Q(n377_2_q));
  _153 u_153_1 (
    .a(n377_2_q[4]), .b(n377_2_q[5]), ._1g(1'b0), ._1c0(1'b0), ._1c1(1'b0), ._1c2(1'b0), ._1c3(1'b1),
    ._2g(1'b0), ._2c0(1'b1), ._2c1(1'b0), ._2c2(n377_1_q[0]), ._2c3(1'b0), ._1y(n153_1__1y), ._2y(n153_1__2y));
  Register register_1 (.clk(clk), .Q(nA), .nwe(_32_2_out), .D(nData));
  ALU alu_1 (.S(n377_2_q[3:0]), .m(n153_1__1y), .cout(c), .zero(z), .nA(nA), .nB(nB), .nF(nF), .cin(n153_1__2y));
  Register register_2 (.clk(clk), .Q(nB), .nwe(_32_3_out), .D(nF));
  OC_Buffer oc_buffer_1 (.ng(_32_out), .In(nF), .Out(nData_2));

  assign nn = nF[15];
endmodule

// OCB
module OC_Buffer (
  input  [15:0] In,
  input  ng,
  output [15:0] Out
);

  _641 u_641_1 (.a_b(1'b1), .ng(ng), .A(In[7:0]), .B(Out[7:0]), .A_2(In[7:0]), .B_2(Out[7:0]));
  _641 u_641_2 (.a_b(1'b1), .ng(ng), .A(In[15:8]), .B(Out[15:8]), .A_2(In[15:8]), .B_2(Out[15:8]));
endmodule

// OCT
module OC_Transceiver (
  input  [15:0] A,
  input  a_b,
  input  ng,
  input  [15:0] B,
  output [15:0] A_2,
  output [15:0] B_2
);

  _641 u_641_1 (.a_b(a_b), .ng(ng), .A(A[7:0]), .B(B[7:0]), .A_2(A_2[7:0]), .B_2(B_2[7:0]));
  _641 u_641_2 (.a_b(a_b), .ng(ng), .A(A[15:8]), .B(B[15:8]), .A_2(A_2[15:8]), .B_2(B_2[15:8]));
endmodule

// Reg
module Register (
  input  [15:0] D,
  input  clk,
  input  nwe,
  output [15:0] Q
);

  _377 u_377_1 (.clk(clk), .ng(nwe), .D(D[7:0]), .Q(Q[7:0]));
  _377 u_377_2 (.clk(clk), .ng(nwe), .D(D[15:8]), .Q(Q[15:8]));
endmodule

// Ctr
module Counter (
  input  [15:0] P,
  input  clk,
  input  nwe,
  input  u_d,
  input  nce,
  output ntc,
  output [15:0] Q
);

  wire n169_1_ntc, n169_2_ntc, n169_3_ntc;

  _169 u_169_1 (.clk(clk), .npe(nwe), .u_d(u_d), .ncet(nce), .ncep(nce), .ntc(n169_1_ntc), .P(P[3:0]), .Q(Q[3:0]));
  _169 u_169_2 (
    .clk(clk), .npe(nwe), .u_d(u_d), .ncet(nce), .ncep(n169_1_ntc), .ntc(n169_2_ntc), .P(P[7:4]), .Q(Q[7:4]));
  _169 u_169_3 (
    .clk(clk), .npe(nwe), .u_d(u_d), .ncet(n169_2_ntc), .ncep(n169_1_ntc), .ntc(n169_3_ntc), .P(P[11:8]),
    .Q(Q[11:8]));
  _169 u_169_4 (
    .clk(clk), .npe(nwe), .u_d(u_d), .ncet(n169_3_ntc), .ncep(n169_1_ntc), .ntc(ntc), .P(P[15:12]),
    .Q(Q[15:12]));
endmodule

module ALU (
  input  [15:0] nA,
  input  [15:0] nB,
  input  [3:0] S,
  input  m,
  input  cin,
  output cout,
  output zero,
  output [15:0] nF
);

  wire n181_1_ng, n181_1_np, n181_2_ng, n181_2_np, n181_3_ng, n181_3_np, n181_4_ng, n181_4_np, n182_1_cn_x,
       n182_1_cn_y, n182_1_cn_z;

  _181 u_181_1 (
    .S(S), .cn(cin), .m(m), .ng(n181_1_ng), .np(n181_1_np), .zero(zero), .nA(nA[3:0]), .nB(nB[3:0]),
    .nF(nF[3:0]));  // open: cn_4
  _181 u_181_2 (
    .S(S), .cn(n182_1_cn_x), .m(m), .ng(n181_2_ng), .np(n181_2_np), .zero(zero), .nA(nA[7:4]), .nB(nB[7:4]),
    .nF(nF[7:4]));  // open: cn_4
  _181 u_181_3 (
    .S(S), .cn(n182_1_cn_y), .m(m), .ng(n181_3_ng), .np(n181_3_np), .zero(zero), .nA(nA[11:8]),
    .nB(nB[11:8]), .nF(nF[11:8]));  // open: cn_4
  _182 u_182_1 (
    .cn(cin), .ng0(n181_1_ng), .np0(n181_1_np), .ng1(n181_2_ng), .np1(n181_2_np), .ng2(n181_3_ng),
    .np2(n181_3_np), .ng3(n181_4_ng), .np3(n181_4_np), .cn_x(n182_1_cn_x), .cn_y(n182_1_cn_y),
    .cn_z(n182_1_cn_z));  // open: ng, np
  _181 u_181_4 (
    .S(S), .cn(n182_1_cn_z), .m(m), .ng(n181_4_ng), .np(n181_4_np), .cn_4(cout), .zero(zero), .nA(nA[15:12]),
    .nB(nB[15:12]), .nF(nF[15:12]));
  Pull_Resistor #(.pull(1)) pull_resistor_1 (.node(zero));
endmodule

module _138 (
  input  a,
  input  b,
  input  c,
  input  g1,
  input  ng2a,
  input  ng2b,
  output ny0,
  output ny1,
  output ny2,
  output ny3,
  output ny4,
  output ny5,
  output ny6,
  output ny7
);

  wire and_1_out;

  and and_1 (and_1_out, g1, ~ng2a, ~ng2b);  // AND_Gate
  nand nand_1 (ny0, ~a, ~b, ~c, and_1_out);  // NAND_Gate
  nand nand_2 (ny1, a, ~b, ~c, and_1_out);  // NAND_Gate
  nand nand_3 (ny2, ~a, b, ~c, and_1_out);  // NAND_Gate
  nand nand_4 (ny3, a, b, ~c, and_1_out);  // NAND_Gate
  nand nand_5 (ny4, ~a, ~b, c, and_1_out);  // NAND_Gate
  nand nand_6 (ny5, a, ~b, c, and_1_out);  // NAND_Gate
  nand nand_7 (ny6, ~a, b, c, and_1_out);  // NAND_Gate
  nand nand_8 (ny7, a, b, c, and_1_out);
endmodule

module _151 (
  input  a,
  input  b,
  input  c,
  input  ng,
  input  d0,
  input  d1,
  input  d2,
  input  d3,
  input  d4,
  input  d5,
  input  d6,
  input  d7,
  output y,
  output ny
);

  wire and_1_out, and_2_out, and_3_out, and_4_out, and_5_out, and_6_out, and_7_out, and_8_out;

  and and_1 (and_1_out, d0, ~a, ~b, ~c, ~ng);  // AND_Gate
  and and_2 (and_2_out, d1, a, ~b, ~c, ~ng);  // AND_Gate
  and and_3 (and_3_out, d2, ~a, b, ~c, ~ng);  // AND_Gate
  and and_4 (and_4_out, d3, a, b, ~c, ~ng);  // AND_Gate
  and and_5 (and_5_out, d4, ~a, ~b, c, ~ng);  // AND_Gate
  and and_6 (and_6_out, d5, a, ~b, c, ~ng);  // AND_Gate
  and and_7 (and_7_out, d6, ~a, b, c, ~ng);  // AND_Gate
  and and_8 (and_8_out, d7, a, b, c, ~ng);  // AND_Gate
  or or_1 (y, and_1_out, and_2_out, and_3_out, and_4_out, and_5_out, and_6_out, and_7_out, and_8_out);
  not not_1 (ny, y);
endmodule

module _153 (
  input  a,
  input  b,
  input  _1g,
  input  _1c0,
  input  _1c1,
  input  _1c2,
  input  _1c3,
  input  _2g,
  input  _2c0,
  input  _2c1,
  input  _2c2,
  input  _2c3,
  output _1y,
  output _2y
);

  wire and_1_out, and_2_out, and_3_out, and_4_out, and_5_out, and_6_out, and_7_out, and_8_out;

  and and_1 (and_1_out, ~_1g, ~a, ~b, _1c0);  // AND_Gate
  and and_2 (and_2_out, ~_1g, a, ~b, _1c1);  // AND_Gate
  and and_3 (and_3_out, ~_1g, ~a, b, _1c2);  // AND_Gate
  and and_4 (and_4_out, ~_1g, a, b, _1c3);  // AND_Gate
  and and_5 (and_5_out, ~_2g, ~a, ~b, _2c0);  // AND_Gate
  and and_6 (and_6_out, ~_2g, a, ~b, _2c1);  // AND_Gate
  and and_7 (and_7_out, ~_2g, ~a, b, _2c2);  // AND_Gate
  and and_8 (and_8_out, ~_2g, a, b, _2c3);  // AND_Gate
  or or_1 (_1y, and_1_out, and_2_out, and_3_out, and_4_out);
  or or_2 (_2y, and_5_out, and_6_out, and_7_out, and_8_out);
endmodule

module _169 (
  input  [3:0] P,
  input  clk,
  input  npe,
  input  u_d,
  input  ncet,
  input  ncep,
  output ntc,
  output [3:0] Q
);

  wire and_1_out, and_2_out, and_3_out, and_4_out, and_5_out, and_6_out, and_7_out, and_8_out, and_9_out,
       and_10_out, and_11_out, and_12_out, and_13_out, and_14_out, and_15_out, and_16_out, and_17_out,
       and_18_out, and_19_out, and_20_out, and_21_out, or_1_out, or_2_out, or_3_out, or_4_out, or_5_out,
       or_6_out, or_7_out, or_8_out, or_9_out, or_10_out;

  and and_1 (and_1_out, ~ncet, ~ncep);  // AND_Gate
  and and_2 (and_2_out, ~npe, P[0]);  // AND_Gate
  and and_3 (and_3_out, ~Q[0], and_1_out, npe);  // AND_Gate
  or or_1 (or_1_out, and_3_out, and_2_out, and_5_out);
  and and_4 (and_4_out, Q[0], ~Q[1], and_1_out, u_d, npe);  // AND_Gate
  and and_5 (and_5_out, Q[0], ~and_1_out, npe);  // AND_Gate
  D_Flip_Flop d_ff_1 (.clk(clk), .D(or_1_out), .Q(Q[0]));  // open: Qn, preset, en, reset
  and and_6 (and_6_out, ~npe, P[1]);  // AND_Gate
  or or_2 (or_2_out, ~and_1_out, ~Q[0]);  // OR_Gate
  and and_7 (and_7_out, or_2_out, Q[1], u_d, npe);
  or or_3 (or_3_out, and_4_out, and_7_out, and_6_out, and_8_out, and_10_out);
  or or_4 (or_4_out, ~and_1_out, Q[0]);  // OR_Gate
  and and_8 (and_8_out, ~Q[0], ~Q[1], and_1_out, ~u_d, npe);  // AND_Gate
  D_Flip_Flop d_ff_2 (.clk(clk), .D(or_3_out), .Q(Q[1]));  // open: Qn, preset, en, reset
  and and_9 (and_9_out, Q[0], Q[1], ~Q[2], and_1_out, u_d, npe);  // AND_Gate
  and and_10 (and_10_out, or_4_out, Q[1], ~u_d, npe);  // AND_Gate
  or or_5 (or_5_out, ~and_1_out, ~Q[0], ~Q[1]);  // OR_Gate
  and and_11 (and_11_out, or_5_out, Q[2], u_d, npe);
  and and_12 (and_12_out, ~npe, P[2]);  // AND_Gate
  and and_13 (and_13_out, ~Q[0], ~Q[1], ~Q[2], and_1_out, ~u_d, npe);  // AND_Gate
  or or_6 (or_6_out, and_9_out, and_11_out, and_12_out, and_13_out, and_14_out);
  D_Flip_Flop d_ff_3 (.clk(clk), .D(or_6_out), .Q(Q[2]));  // open: Qn, preset, en, reset
  or or_7 (or_7_out, ~and_1_out, Q[0], Q[1]);  // OR_Gate
  and and_14 (and_14_out, or_7_out, Q[2], ~u_d, npe);  // AND_Gate
  or or_8 (or_8_out, ~and_1_out, ~Q[0], ~Q[1], ~Q[2]);  // OR_Gate
  and and_15 (and_15_out, Q[0], Q[1], Q[2], ~Q[3], and_1_out, u_d, npe);  // AND_Gate
  and and_16 (and_16_out, ~npe, P[3]);  // AND_Gate
  and and_17 (and_17_out, or_8_out, Q[3], u_d, npe);
  or or_9 (or_9_out, and_15_out, and_17_out, and_16_out, and_18_out, and_19_out);
  or or_10 (or_10_out, ~and_1_out, Q[0], Q[1], Q[2]);  // OR_Gate
  and and_18 (and_18_out, ~Q[0], ~Q[1], ~Q[2], ~Q[3], and_1_out, ~u_d, npe);  // AND_Gate
  D_Flip_Flop d_ff_4 (.clk(clk), .D(or_9_out), .Q(Q[3]));  // open: Qn, preset, en, reset
  and and_19 (and_19_out, or_10_out, Q[3], ~u_d, npe);  // AND_Gate
  and and_20 (and_20_out, u_d, ~ncet, Q[0], Q[1], Q[2], Q[3]);  // AND_Gate
  and and_21 (and_21_out, ~u_d, ~ncet, ~Q[0], ~Q[1], ~Q[2], ~Q[3]);  // AND_Gate
  nor nor_1 (ntc, and_20_out, and_21_out);
endmodule

module _181 (
  input  [3:0] nA,
  input  [3:0] nB,
  input  [3:0] S,
  input  m,
  input  cn,
  output cn_4,
  output zero,
  output ng,
  output np,
  output [3:0] nF
);

  wire and_1_out, and_2_out, and_3_out, and_4_out, and_5_out, and_6_out, and_7_out, and_8_out, and_9_out,
       and_10_out, and_11_out, and_12_out, and_13_out, and_14_out, and_15_out, and_16_out, and_17_out,
       and_18_out, and_19_out, and_20_out, and_21_out, and_22_out, and_23_out, and_24_out, and_26_out,
       and_27_out, and_28_out, and_29_out, nand_1_out, nand_3_out, nor_1_out, nor_2_out, nor_3_out,
       nor_4_out, nor_5_out, nor_6_out, nor_7_out, nor_8_out, nor_9_out, nor_10_out, nor_11_out, not_1_out,
       xor_2_out, xor_3_out, xor_5_out, xor_8_out;

  and and_1 (and_1_out, nB[0], S[0]);
  nor nor_1 (nor_1_out, nA[0], and_1_out, and_2_out);
  not not_1 (not_1_out, m);
  nand nand_1 (nand_1_out, cn, not_1_out);
  xor xor_1 (nF[0], nand_1_out, xor_2_out);
  and and_2 (and_2_out, ~nB[0], S[1]);  // AND_Gate
  and and_3 (and_3_out, nA[0], ~nB[0], S[2]);  // AND_Gate
  and and_4 (and_4_out, cn, nor_3_out, not_1_out);
  and and_5 (and_5_out, nor_1_out, not_1_out);
  nor nor_2 (nor_2_out, and_5_out, and_4_out);
  xor xor_2 (xor_2_out, nor_1_out, nor_3_out);
  and and_6 (and_6_out, nB[1], S[0]);
  and and_7 (and_7_out, nA[0], nB[0], S[3]);
  nor nor_3 (nor_3_out, and_3_out, and_7_out);
  nor nor_4 (nor_4_out, nA[1], and_6_out, and_9_out);
  and and_8 (and_8_out, nor_4_out, not_1_out);
  xor xor_3 (xor_3_out, nor_4_out, nor_7_out);
  xor xor_4 (nF[1], nor_2_out, xor_3_out);
  and and_9 (and_9_out, ~nB[1], S[1]);  // AND_Gate
  and and_10 (and_10_out, nA[1], ~nB[1], S[2]);  // AND_Gate
  and and_11 (and_11_out, cn, nor_3_out, nor_7_out, not_1_out);
  and and_12 (and_12_out, nor_1_out, nor_7_out, not_1_out);
  nor nor_5 (nor_5_out, and_8_out, and_12_out, and_11_out);
  and and_13 (and_13_out, nB[2], S[0]);
  and and_14 (and_14_out, nA[1], nB[1], S[3]);
  nor nor_6 (nor_6_out, nA[2], and_13_out, and_17_out);
  nor nor_7 (nor_7_out, and_10_out, and_14_out);
  and and_15 (and_15_out, nor_6_out, not_1_out);
  xor xor_5 (xor_5_out, nor_6_out, nor_9_out);
  xor xor_6 (nF[2], nor_5_out, xor_5_out);
  and and_16 (and_16_out, nA[2], ~nB[2], S[2]);  // AND_Gate
  and and_17 (and_17_out, ~nB[2], S[1]);  // AND_Gate
  and and_18 (and_18_out, nor_1_out, nor_7_out, nor_9_out, not_1_out);
  and and_19 (and_19_out, nor_4_out, nor_9_out, not_1_out);
  nor nor_8 (nor_8_out, and_15_out, and_19_out, and_18_out, and_22_out);
  and and_20 (and_20_out, nB[3], S[0]);
  and and_21 (and_21_out, nA[2], nB[2], S[3]);
  nor nor_9 (nor_9_out, and_16_out, and_21_out);
  nor nor_10 (nor_10_out, nA[3], and_20_out, and_24_out);
  and and_22 (and_22_out, cn, nor_3_out, nor_7_out, nor_9_out, not_1_out);
  xor xor_7 (nF[3], nor_8_out, xor_8_out);
  and and_23 (and_23_out, nA[3], ~nB[3], S[2]);  // AND_Gate
  and and_24 (and_24_out, ~nB[3], S[1]);  // AND_Gate
  nand nand_2 (np, nor_3_out, nor_7_out, nor_9_out, nor_11_out);
  xor xor_8 (xor_8_out, nor_10_out, nor_11_out);
  and and_25 (zero, nF[0], nF[1], nF[2], nF[3]);
  and and_26 (and_26_out, nA[3], nB[3], S[3]);
  nor nor_11 (nor_11_out, and_23_out, and_26_out);
  nand nand_3 (nand_3_out, cn, nor_3_out, nor_7_out, nor_9_out, nor_11_out);
  and and_27 (and_27_out, nor_4_out, nor_9_out, nor_11_out);
  and and_28 (and_28_out, nor_1_out, nor_7_out, nor_9_out, nor_11_out);
  nor nor_12 (ng, and_28_out, and_27_out, and_29_out, nor_10_out);
  and and_29 (and_29_out, nor_6_out, nor_11_out);
  or or_1 (cn_4, ~nand_3_out, ~ng);  // OR_Gate

  // Notes on the sheet:
  //   and_25 drives only 0 and floats otherwise
endmodule

module _182 (
  input  ng0,
  input  np0,
  input  ng1,
  input  np1,
  input  ng2,
  input  np2,
  input  ng3,
  input  np3,
  input  cn,
  output cn_x,
  output cn_y,
  output cn_z,
  output ng,
  output np
);

  wire and_1_out, and_2_out, and_3_out, and_4_out, and_5_out, and_6_out, and_7_out, and_8_out, and_9_out,
       and_10_out, and_11_out, and_12_out, and_13_out, not_1_out;

  not not_1 (not_1_out, cn);
  and and_1 (and_1_out, ng0, np0);
  and and_2 (and_2_out, ng0, not_1_out);
  nor nor_1 (cn_x, and_1_out, and_2_out);
  and and_3 (and_3_out, ng0, np0, ng1);
  and and_4 (and_4_out, ng1, np1);
  nor nor_2 (cn_y, and_4_out, and_3_out, and_5_out);
  and and_5 (and_5_out, ng0, ng1, not_1_out);
  and and_6 (and_6_out, ng1, np1, ng2);
  and and_7 (and_7_out, ng2, np2);
  nor nor_3 (cn_z, and_7_out, and_6_out, and_8_out, and_10_out);
  and and_8 (and_8_out, ng0, np0, ng1, ng2);
  and and_9 (and_9_out, ng3, np3);
  and and_10 (and_10_out, ng0, ng1, ng2, not_1_out);
  and and_11 (and_11_out, ng2, np2, ng3);
  or or_1 (ng, and_9_out, and_11_out, and_13_out, and_12_out);
  and and_12 (and_12_out, ng0, ng1, ng2, ng3);
  and and_13 (and_13_out, ng1, np1, ng2, ng3);
  or or_2 (np, np0, np1, np2, np3);
endmodule

module _377 (
  input  [7:0] D,
  input  clk,
  input  ng,
  output [7:0] Q
);

  wire and_1_out, and_2_out;

  and and_1 (and_1_out, clk, ~and_2_out);  // AND_Gate
  and and_2 (and_2_out, ~and_1_out, ~ng);  // AND_Gate
  D_Flip_Flop d_ff_1 (.clk(clk), .D(D[0]), .Q(Q[0]), .en(and_2_out));  // open: Qn, preset, reset
  D_Flip_Flop d_ff_2 (.clk(clk), .D(D[1]), .Q(Q[1]), .en(and_2_out));  // open: Qn, preset, reset
  D_Flip_Flop d_ff_3 (.clk(clk), .D(D[2]), .Q(Q[2]), .en(and_2_out));  // open: Qn, preset, reset
  D_Flip_Flop d_ff_4 (.clk(clk), .D(D[3]), .Q(Q[3]), .en(and_2_out));  // open: Qn, preset, reset
  D_Flip_Flop d_ff_5 (.clk(clk), .D(D[4]), .Q(Q[4]), .en(and_2_out));  // open: Qn, preset, reset
  D_Flip_Flop d_ff_6 (.clk(clk), .D(D[5]), .Q(Q[5]), .en(and_2_out));  // open: Qn, preset, reset
  D_Flip_Flop d_ff_7 (.clk(clk), .D(D[6]), .Q(Q[6]), .en(and_2_out));  // open: Qn, preset, reset
  D_Flip_Flop d_ff_8 (.clk(clk), .D(D[7]), .Q(Q[7]), .en(and_2_out));  // open: Qn, preset, reset
endmodule

module _641 (
  input  [7:0] A,
  input  a_b,
  input  ng,
  input  [7:0] B,
  output [7:0] A_2,
  output [7:0] B_2
);

  wire and_1_out, and_2_out;

  and and_1 (and_1_out, a_b, ~ng);  // AND_Gate
  nand nand_1 (B_2[0], and_1_out, ~A[0]);  // NAND_Gate
  and and_2 (and_2_out, ~a_b, ~ng);  // AND_Gate
  nand nand_2 (A_2[0], and_2_out, ~B[0]);  // NAND_Gate
  nand nand_3 (B_2[1], and_1_out, ~A[1]);  // NAND_Gate
  nand nand_4 (A_2[1], and_2_out, ~B[1]);  // NAND_Gate
  nand nand_5 (B_2[2], and_1_out, ~A[2]);  // NAND_Gate
  nand nand_6 (A_2[2], and_2_out, ~B[2]);  // NAND_Gate
  nand nand_7 (B_2[3], and_1_out, ~A[3]);  // NAND_Gate
  nand nand_8 (A_2[3], and_2_out, ~B[3]);  // NAND_Gate
  nand nand_9 (B_2[4], and_1_out, ~A[4]);  // NAND_Gate
  nand nand_10 (A_2[4], and_2_out, ~B[4]);  // NAND_Gate
  nand nand_11 (B_2[5], and_1_out, ~A[5]);  // NAND_Gate
  nand nand_12 (A_2[5], and_2_out, ~B[5]);  // NAND_Gate
  nand nand_13 (B_2[6], and_1_out, ~A[6]);  // NAND_Gate
  nand nand_14 (A_2[6], and_2_out, ~B[6]);  // NAND_Gate
  nand nand_15 (B_2[7], and_1_out, ~A[7]);  // NAND_Gate
  nand nand_16 (A_2[7], and_2_out, ~B[7]);  // NAND_Gate

  // Notes on the sheet:
  //   nand_1 drives only 0 and floats otherwise
  //   nand_2 drives only 0 and floats otherwise
  //   nand_3 drives only 0 and floats otherwise
  //   nand_4 drives only 0 and floats otherwise
  //   nand_5 drives only 0 and floats otherwise
  //   nand_6 drives only 0 and floats otherwise
  //   nand_7 drives only 0 and floats otherwise
  //   nand_8 drives only 0 and floats otherwise
  //   nand_9 drives only 0 and floats otherwise
  //   nand_10 drives only 0 and floats otherwise
  //   nand_11 drives only 0 and floats otherwise
  //   nand_12 drives only 0 and floats otherwise
  //   nand_13 drives only 0 and floats otherwise
  //   nand_14 drives only 0 and floats otherwise
  //   nand_15 drives only 0 and floats otherwise
  //   nand_16 drives only 0 and floats otherwise
endmodule

module _62256 (
  input  [7:0] D,
  input  clk,
  input  ncs,
  input  noe,
  input  nwe,
  input  [14:0] A,
  output [7:0] D_2
);

  wire and_1_out, and_2_out, not_1_out;
  wire [7:0] controlled_buffer_1_out;

  and and_1 (and_1_out, ~ncs, ~noe, nwe);  // AND_Gate
  and and_2 (and_2_out, ~ncs, ~nwe);  // AND_Gate
  not not_1 (not_1_out, and_2_out);
  assign controlled_buffer_1_out = and_2_out ? D : 8'bz;  // Controlled_Buffer controlled_buffer_1
  RAM #(.addrWidth(15)) ram_1 (
    .addr(A), .data(controlled_buffer_1_out), .clk(clk), .ld(not_1_out), .clr(1'b0));  // open: sel
  assign D_2 = and_1_out ? controlled_buffer_1_out : 8'bz;  // Controlled_Buffer controlled_buffer_2
endmodule
