// Logisim project CPU-modified.circ as structural Verilog: 18 circuits, main circuit CPU
module CPU (
  input  run,
  input  step,
  input  al,
  input  exam,
  input  dep,
  input  [15:0] S
);

  wire alu_board_1_p10, clock_1_out, control_board_1_p13, control_board_1_p14, control_board_1_p15,
       control_board_1_p16, not_3_out, not_5_out, not_6_out, not_7_out, not_10_out, not_12_out, not_13_out,
       not_16_out, ram_decoder_board_1__0xxx, ram_decoder_board_1__1xxx;
  wire [1:0] alu_board_1_p3;
  wire [6:0] control_board_1_p12, not_11_out;
  wire [15:0] alu_board_1_p7, alu_board_1_p8, alu_board_1_p9, not_1_out, not_2_out, not_4_out, not_8_out,
       not_9_out, not_14_out, not_15_out, not_17_out, not_18_out, pull_resistor_1_node, pull_resistor_2_node,
       undriven, undriven_2;

  Pull_Resistor #(.pull(1)) pull_resistor_1 (.node(pull_resistor_1_node));
  Clock clock_1 (.out(clock_1_out));
  assign not_1_out = ~pull_resistor_1_node;  // NOT_Gate not_1, 16 bits wide
  // Probe on not_1_out
  Pull_Resistor #(.pull(1)) pull_resistor_2 (.node(pull_resistor_2_node));
  assign not_2_out = ~pull_resistor_2_node;  // NOT_Gate not_2, 16 bits wide
  // Probe on not_2_out
  RAM_Decoder_Board ram_decoder_board_1 (
    ._0xxx(ram_decoder_board_1__0xxx), ._1xxx(ram_decoder_board_1__1xxx), .nAddress(pull_resistor_2_node),
    .nr_w(alu_board_1_p3));  // open: _2xxx, _3xxx, _4xxx, _5xxx, _6xxx, _7xxx
  not not_3 (not_3_out, run);
  // ALU_Board alu_board_1: pin names not known; wires that end beside it: clock_1_out, ram_decoder_board_1__1xxx, alu_board_1_p3, pull_resistor_1_node, pull_resistor_2_node, pull_resistor_1_node, alu_board_1_p7, alu_board_1_p8, alu_board_1_p9, alu_board_1_p10
  assign not_4_out = ~alu_board_1_p7;  // NOT_Gate not_4, 16 bits wide
  // Probe on not_4_out
  not not_5 (not_5_out, al);
  not not_6 (not_6_out, step);
  not not_7 (not_7_out, exam);
  assign not_8_out = ~alu_board_1_p9;  // NOT_Gate not_8, 16 bits wide
  assign not_9_out = ~alu_board_1_p8;  // NOT_Gate not_9, 16 bits wide
  // Probe on not_8_out
  // Probe on not_9_out
  not not_10 (not_10_out, dep);
  // Control_Board control_board_1: pin names not known; wires that end beside it: clock_1_out, ram_decoder_board_1__0xxx, not_3_out, not_6_out, not_5_out, not_7_out, not_10_out, alu_board_1_p10, alu_board_1_p3, pull_resistor_2_node, pull_resistor_2_node, control_board_1_p12, control_board_1_p13, control_board_1_p14, control_board_1_p15, control_board_1_p16, alu_board_1_p3, alu_board_1_p3, alu_board_1_p3
  assign not_11_out = ~control_board_1_p12;  // NOT_Gate not_11, 7 bits wide
  // Probe on not_11_out
  not not_12 (not_12_out, control_board_1_p14);
  not not_13 (not_13_out, control_board_1_p15);
  // Probe on not_12_out
  // Probe on not_13_out
  assign not_14_out = ~S;  // NOT_Gate not_14, 16 bits wide
  Register_Board register_board_1 ();
  assign not_15_out = ~undriven;  // NOT_Gate not_15, 16 bits wide
  not not_16 (not_16_out, control_board_1_p16);
  // Probe on not_16_out
  // Probe on not_15_out
  assign not_17_out = ~undriven_2;  // NOT_Gate not_17, 16 bits wide
  assign not_18_out = ~undriven;  // NOT_Gate not_18, 16 bits wide
  // Probe on not_17_out
  // Probe on not_18_out
endmodule

module Control_Board (
  input  clk,
  input  clk_2,
  input  ng,
  input  [1:0] nr_w,
  input  nrun,
  input  nstep,
  input  nal,
  input  nexam,
  input  c,
  input  ndep,
  input  [15:0] nAddress,
  input  ng_2,
  input  [2:0] flags,
  input  [15:0] nAddress_2,
  output neF,
  output nwA,
  output nwB,
  output [3:0] S,
  output m,
  output cin,
  output [1:0] nr_w_2,
  output nc,
  output nz,
  output nn,
  output ns_d,
  output nd_t,
  output nt_d,
  output nd_x,
  output nx_plus,
  output nx_a,
  output nd_p,
  output np_d,
  output np_a,
  output [6:0] nState
);

  wire _04_3_out, _11_3_out, _21_2_out, _21_out, _32_2_out, _32_3_out, _32_4_out, _32_7_out, _32_11_out,
       _32_out, _40_2_out, _40_out, n151_1_p13, n377_1_nq7, undriven, undriven_2, undriven_3, undriven_4,
       undriven_5;
  wire [7:1] n377_3_p5;
  wire [7:4] n377_2_p8;

  not _04 (nc, flags[0]);
  not _04_2 (nz, flags[1]);
  not _04_3 (_04_3_out, flags[2]);
  nand _40 (_40_out, nstep, nal, nexam, ndep);
  // _151 151_1: pin names not known; wires that end beside it: ng_2, flags[2], flags[2], flags[2], flags[2], _04_3_out, nz, flags[1], nc, flags[0], flags[2], 1'b1, n151_1_p13
  _377 u_377_1 (
    .CLK(clk_2), .nG(1'b0), .nD0(_32_7_out), .nQ0(nState[6]), .nD1(nState[6]), .nQ1(nState[5]),
    .nD2(nState[5]), .nD3(nState[4]), .nQ2(nState[4]), .nQ3(nState[3]), .nD4(_32_2_out), .nD5(_32_3_out),
    .nD6(_32_4_out), .nD7(_40_out), .nQ4(nState[2]), .nQ5(nState[1]), .nQ6(nState[0]), .nQ7(n377_1_nq7));
  nand _40_2 (_40_2_out, 1'b1, nState[6], nState[5], nState[4]);
  or _32 (_32_out, n377_1_nq7, nstep);
  or _32_2 (_32_2_out, n377_1_nq7, nal);
  or _32_3 (_32_3_out, n377_1_nq7, nexam);
  or _32_4 (_32_4_out, n377_1_nq7, ndep);
  and _21 (_21_out, nState[6], nState[5], nState[4], nState[1]);
  and _21_2 (_21_2_out, nState[3], nState[0], 1'b1, 1'b1);
  and _08 (ns_d, nState[2], nState[0]);
  and _08_2 (nd_t, nState[5], nState[1]);
  and _11 (nd_x, nState[6], nState[4], nState[2]);
  and _08_3 (nx_plus, nState[1], nState[0]);
  and _11_2 (nx_a, undriven_3, nState[5], nState[1]);
  or _32_5 (nd_p, undriven_4, undriven_5);
  or _32_6 (np_d, undriven, undriven_2);
  and _08_4 (np_a, nState[4], nState[6]);
  or _32_7 (_32_7_out, _40_2_out, _11_3_out);
  and _11_3 (_11_3_out, nrun, 1'b1, _32_out);
  or _32_8 (neF, ng, nr_w[0]);
  or _32_9 (clk, ng, nr_w[1]);
  or _32_10 (nwB, clk, nAddress[6]);
  or _32_11 (_32_11_out, clk, nAddress[7]);
  // _377 377_2: pin names not known; wires that end beside it: clk, clk, clk, clk, nwB, neF, {2'b00, nAddress[5:0]}, {n377_2_p8, S}, clk, nwB
  // _377 377_3: pin names not known; wires that end beside it: clk, clk, _32_11_out, {{7{1'b0}}, c}, {n377_3_p5, 1'b1}, n377_3_p5, 1'b1, 1'b1
  _153 u_153_1 (
    ._2G(1'b1), ._2C0(1'b1), ._2C1(1'b1), ._2C2(1'b1));  // open: A, B, _1G, _1C0, _1C1, _1C2, _1C3, _2C3, _1Y, _2Y

  assign nAddress_2[2:0] = {3{flags[2]}};
  assign nn = flags[2];
  assign nt_d = nState[3];
  assign nwA = clk;
  // also tied to GND on the sheet: flags[2]
endmodule

// Reg Board
module Register_Board (
);

  wire CLK, n377_1_nq0, n377_1_nq1, n377_1_nq2, n377_1_nq3, n377_1_nq4, n377_1_nq5, n377_1_nq6, n377_1_nq7,
       n641_1_nb0_2, n641_1_nb1_2, n641_1_nb2_2, n641_1_nb3_2, n641_1_nb4_2, n641_1_nb5_2, n641_1_nb6_2,
       n641_1_nb7_2, nD0i, nD1i, nD2i, nD3i, nD4i, nD5i, nD6i, nD7i, nD_T, nT_D;

  _377 u_377_1 (
    .CLK(CLK), .nG(nD_T), .nD0(nD0i), .nQ0(n377_1_nq0), .nD1(nD1i), .nQ1(n377_1_nq1), .nD2(nD2i), .nD3(nD3i),
    .nQ2(n377_1_nq2), .nQ3(n377_1_nq3), .nD4(nD4i), .nD5(nD5i), .nD6(nD6i), .nD7(nD7i), .nQ4(n377_1_nq4),
    .nQ5(n377_1_nq5), .nQ6(n377_1_nq6), .nQ7(n377_1_nq7));
  _641 u_641_1 (
    .nG(nT_D), .nA0(n377_1_nq0), .nA0_2(n377_1_nq0), .nB0(n641_1_nb0_2), .nB0_2(n641_1_nb0_2),
    .nA1(n377_1_nq1), .nA1_2(n377_1_nq1), .nB1(n641_1_nb1_2), .nB1_2(n641_1_nb1_2), .nA2(n377_1_nq2),
    .nA2_2(n377_1_nq2), .nA3(n377_1_nq3), .nA3_2(n377_1_nq3), .nB2(n641_1_nb2_2), .nB2_2(n641_1_nb2_2),
    .nB3(n641_1_nb3_2), .nB3_2(n641_1_nb3_2), .nA4(n377_1_nq4), .nA4_2(n377_1_nq4), .nA5(n377_1_nq5),
    .nA5_2(n377_1_nq5), .nA6(n377_1_nq6), .nA6_2(n377_1_nq6), .nA7_2(n377_1_nq7), .nB4(n641_1_nb4_2),
    .nB4_2(n641_1_nb4_2), .nB5(n641_1_nb5_2), .nB5_2(n641_1_nb5_2), .nB6(n641_1_nb6_2), .nB6_2(n641_1_nb6_2),
    .nB7(n641_1_nb7_2), .nB7_2(n641_1_nb7_2), .nA7(n377_1_nq7), .A_B(1'b1));
  // Probe on n377_1_nq0
  // Probe on n377_1_nq1
  // Probe on n377_1_nq2
  // Probe on n377_1_nq3
  // Probe on n377_1_nq4
  // Probe on n377_1_nq5
  // Probe on n377_1_nq6
  // Probe on n377_1_nq7
endmodule

// RAM&Decoder
module RAM_Decoder_Board (
  input  [1:0] nr_w,
  input  [15:0] nAddress,
  output _0xxx,
  output _1xxx,
  output _2xxx,
  output _3xxx,
  output _4xxx,
  output _5xxx,
  output _6xxx,
  output _7xxx
);

  wire A0, A1, A2, A3, A4, A5, A6, A7, A8, A9, Aa, Ab, Ac, Ad, Ae, Af, CLK, D0, D1, D2, D3, D4, D5, D6, D7,
       D8, D9, Da, Db, Dc, Dd, De, Df, n153_1_p7, n153_2_p2, n153_2_p3, n153_2_p4, n641_1_nb2_2,
       n641_1_nb3_2, n641_1_nb4_2, n641_1_nb5_2, n641_1_nb6_2, n641_2_nb0_2, n641_2_nb1_2, n641_2_nb2_2,
       n641_2_nb3_2, n641_2_nb4_2, n641_2_nb5_2, n641_2_nb6_2, n641_2_nb7_2, nR, nW, undriven, undriven_2;

  // _153 153_1: pin names not known; wires that end beside it: nr_w[1], nAddress[15], nAddress[15], nAddress[15], 1'b0, nAddress[15], n153_1_p7
  OC_Transceiver oc_transceiver_1 (.ng(n153_1_p7), .a_b(undriven));  // open: A, A_2, B_2, B
  // _153 153_2: pin names not known; wires that end beside it: 1'b0, n153_2_p2, n153_2_p3, n153_2_p4
  _641 u_641_1 (
    .nG(undriven_2), .nA0(D0), .nA0_2(D0), .nB0(n153_2_p3), .nB0_2(n153_2_p3), .nA1(D1), .nA1_2(D1),
    .nB1(n153_2_p4), .nB1_2(n153_2_p4), .nA2(D2), .nA2_2(D2), .nA3(D3), .nA3_2(D3), .nB2(n641_1_nb2_2),
    .nB2_2(n641_1_nb2_2), .nB3(n641_1_nb3_2), .nB3_2(n641_1_nb3_2), .nA4(D4), .nA4_2(D4), .nA5(D5),
    .nA5_2(D5), .nA6(D6), .nA6_2(D6), .nA7_2(D7), .nB4(n641_1_nb4_2), .nB4_2(n641_1_nb4_2),
    .nB5(n641_1_nb5_2), .nB5_2(n641_1_nb5_2), .nB6(n641_1_nb6_2), .nB6_2(n641_1_nb6_2), .nB7(n641_1_nb4_2),
    .nB7_2(n641_1_nb4_2), .nA7(D7), .A_B(n153_2_p2));
  _62256 u_62256_1 (
    .CLK(CLK), .nG(Af), .nW(nW), .nA0(A0), .nA1(A1), .nA2(A2), .nA3(A3), .nA4(A4), .nA5(A5), .nA6(A6),
    .nA7(A7), .nA8(A8), .nA9(A9), .nAa(Aa), .nAb(Ab), .nAc(Ac), .nAd(Ad), .nAe(Ae), .nD1o(n153_2_p3),
    .nD2i(n153_2_p4), .nD2o(n641_1_nb2_2), .nD3i(n641_1_nb3_2), .nD3o(n641_1_nb4_2), .nD4i(n641_1_nb5_2),
    .nD4o(n641_1_nb6_2), .nD5i(n641_1_nb4_2), .nR(nR));  // open: nD0i, nD0o, nD1i, nD5o, nD6i, nD6o, nD7i, nD7o
  Pull_Resistor #(.pull(1)) pull_resistor_1 (.node(n153_2_p3));
  Pull_Resistor #(.pull(1)) pull_resistor_2 (.node(n153_2_p4));
  Pull_Resistor #(.pull(1)) pull_resistor_3 (.node(n641_1_nb3_2));
  Pull_Resistor #(.pull(1)) pull_resistor_4 (.node(n641_1_nb2_2));
  Pull_Resistor #(.pull(1)) pull_resistor_5 (.node(n641_1_nb4_2));
  Pull_Resistor #(.pull(1)) pull_resistor_6 (.node(n641_1_nb6_2));
  Pull_Resistor #(.pull(1)) pull_resistor_7 (.node(n641_1_nb4_2));
  Pull_Resistor #(.pull(1)) pull_resistor_8 (.node(n641_1_nb5_2));
  _641 u_641_2 (
    .nA0(D8), .nA0_2(D8), .nB0(n641_2_nb0_2), .nB0_2(n641_2_nb0_2), .nA1(D9), .nA1_2(D9), .nB1(n641_2_nb1_2),
    .nB1_2(n641_2_nb1_2), .nA2(Da), .nA2_2(Da), .nA3(Db), .nA3_2(Db), .nB2(n641_2_nb2_2),
    .nB2_2(n641_2_nb2_2), .nB3(n641_2_nb3_2), .nB3_2(n641_2_nb3_2), .nA4(Dc), .nA4_2(Dc), .nA5(Dd),
    .nA5_2(Dd), .nA6(De), .nA6_2(De), .nA7_2(Df), .nB4(n641_2_nb4_2), .nB4_2(n641_2_nb4_2),
    .nB5(n641_2_nb5_2), .nB5_2(n641_2_nb5_2), .nB6(n641_2_nb6_2), .nB6_2(n641_2_nb6_2), .nB7(n641_2_nb7_2),
    .nB7_2(n641_2_nb7_2), .nA7(Df));  // open: nG, A_B
  _62256 u_62256_2 (
    .CLK(CLK), .nG(Af), .nW(nW), .nA0(A0), .nA1(A1), .nA2(A2), .nA3(A3), .nA4(A4), .nA5(A5), .nA6(A6),
    .nA7(A7), .nA8(A8), .nA9(A9), .nAa(Aa), .nAb(Ab), .nAc(Ac), .nAd(Ad), .nAe(Ae), .nD1o(n641_2_nb0_2),
    .nD2i(n641_2_nb1_2), .nD2o(n641_2_nb2_2), .nD3i(n641_2_nb3_2), .nD3o(n641_2_nb4_2), .nD4i(n641_2_nb5_2),
    .nD4o(n641_2_nb6_2), .nD5i(n641_2_nb7_2), .nR(nR));  // open: nD0i, nD0o, nD1i, nD5o, nD6i, nD6o, nD7i, nD7o
  Pull_Resistor #(.pull(1)) pull_resistor_9 (.node(n641_2_nb2_2));
  Pull_Resistor #(.pull(1)) pull_resistor_10 (.node(n641_2_nb3_2));
  Pull_Resistor #(.pull(1)) pull_resistor_11 (.node(n641_2_nb0_2));
  Pull_Resistor #(.pull(1)) pull_resistor_12 (.node(n641_2_nb1_2));
  Pull_Resistor #(.pull(1)) pull_resistor_13 (.node(n641_2_nb5_2));
  Pull_Resistor #(.pull(1)) pull_resistor_14 (.node(n641_2_nb7_2));
  Pull_Resistor #(.pull(1)) pull_resistor_15 (.node(n641_2_nb4_2));
  Pull_Resistor #(.pull(1)) pull_resistor_16 (.node(n641_2_nb6_2));
  // _138 138_1: pin names not known; wires that end beside it: n641_2_nb6_2, n641_2_nb6_2, n641_2_nb7_2, 1'b0, _0xxx, 1'b0, _1xxx, nAddress[15], nAddress[15], _2xxx, _3xxx, _4xxx, nAddress[14], _5xxx
  // also tied to VCC on the sheet: nAddress[15]
endmodule

module ALU_Board (
  input  clk,
  input  [15:0] nData,
  input  neF,
  input  nwA,
  input  nwB,
  input  [3:0] S,
  input  m,
  output [15:0] nData_2,
  output [15:0] nA,
  output [15:0] nB,
  output [15:0] nF
);

  wire C, Cin, n181_1_nf0, n181_1_nf1, n181_1_nf2, n181_1_nf3, n181_1_ng, n181_1_np, n181_2_nf0, n181_2_nf1,
       n181_2_nf2, n181_2_nf3, n181_2_ng, n181_2_np, n181_3_nf0, n181_3_nf1, n181_3_nf2, n181_3_nf3,
       n181_3_ng, n181_3_np, n181_4_nf0, n181_4_nf1, n181_4_nf2, n181_4_ng, n181_4_np, n182_1_c1, n182_1_c2,
       n182_1_c3, n377_1_nq0, n377_1_nq1, n377_1_nq2, n377_1_nq3, n377_1_nq4, n377_1_nq5, n377_1_nq6,
       n377_1_nq7, n377_2_nq0, n377_2_nq1, n377_2_nq2, n377_2_nq3, n377_2_nq4, n377_2_nq5, n377_2_nq6,
       n377_2_nq7, n377_3_nq0, n377_3_nq1, n377_3_nq2, n377_3_nq3, n377_3_nq4, n377_3_nq5, n377_3_nq6,
       n377_3_nq7, n377_4_nq0, n377_4_nq1, n377_4_nq2, n377_4_nq3, n377_4_nq4, n377_4_nq5, n377_4_nq6,
       n377_4_nq7, nN, undriven, undriven_2, undriven_3, undriven_4, undriven_5, Z;

  _377 u_377_1 (
    .nQ0(n377_1_nq0), .nQ1(n377_1_nq1), .nQ2(n377_1_nq2), .nQ3(n377_1_nq3), .nQ4(n377_1_nq4),
    .nQ5(n377_1_nq5), .nQ6(n377_1_nq6), .nQ7(n377_1_nq7));  // open: CLK, nG, nD0, nD1, nD2, nD3, nD4, nD5, nD6, nD7
  _181 u_181_1 (
    .Cin(Cin), .M(undriven_5), .nG(n181_1_ng), .nP(n181_1_np), .Z(Z), .S0(undriven), .S1(undriven_2),
    .S2(undriven_3), .S3(undriven_4), .nF0(n181_1_nf0), .nF1(n181_1_nf1), .nF2(n181_1_nf2), .nF3(n181_1_nf3),
    .nA0(n377_1_nq0), .nA1(n377_1_nq1), .nA2(n377_1_nq2), .nA3(n377_1_nq3), .nB0(n377_2_nq0),
    .nB1(n377_2_nq1), .nB2(n377_2_nq2), .nB3(n377_2_nq3));  // open: C
  _377 u_377_2 (
    .nQ0(n377_2_nq0), .nQ1(n377_2_nq1), .nQ2(n377_2_nq2), .nQ3(n377_2_nq3), .nQ4(n377_2_nq4),
    .nQ5(n377_2_nq5), .nQ6(n377_2_nq6), .nQ7(n377_2_nq7));  // open: CLK, nG, nD0, nD1, nD2, nD3, nD4, nD5, nD6, nD7
  _181 u_181_2 (
    .Cin(n182_1_c1), .M(undriven_5), .nG(n181_2_ng), .nP(n181_2_np), .Z(Z), .S0(undriven), .S1(undriven_2),
    .S2(undriven_3), .S3(undriven_4), .nF0(n181_2_nf0), .nF1(n181_2_nf1), .nF2(n181_2_nf2), .nF3(n181_2_nf3),
    .nA0(n377_1_nq4), .nA1(n377_1_nq5), .nA2(n377_1_nq6), .nA3(n377_1_nq7), .nB0(n377_2_nq4),
    .nB1(n377_2_nq5), .nB2(n377_2_nq6), .nB3(n377_2_nq7));  // open: C
  _377 u_377_3 (
    .nQ0(n377_3_nq0), .nQ1(n377_3_nq1), .nQ2(n377_3_nq2), .nQ3(n377_3_nq3), .nQ4(n377_3_nq4),
    .nQ5(n377_3_nq5), .nQ6(n377_3_nq6), .nQ7(n377_3_nq7));  // open: CLK, nG, nD0, nD1, nD2, nD3, nD4, nD5, nD6, nD7
  _181 u_181_3 (
    .Cin(n182_1_c2), .M(undriven_5), .nG(n181_3_ng), .nP(n181_3_np), .Z(Z), .S0(undriven), .S1(undriven_2),
    .S2(undriven_3), .S3(undriven_4), .nF0(n181_3_nf0), .nF1(n181_3_nf1), .nF2(n181_3_nf2), .nF3(n181_3_nf3),
    .nA0(n377_3_nq0), .nA1(n377_3_nq1), .nA2(n377_3_nq2), .nA3(n377_3_nq3), .nB0(n377_4_nq0),
    .nB1(n377_4_nq1), .nB2(n377_4_nq2), .nB3(n377_4_nq3));  // open: C
  _182 u_182_1 (
    .Cin(Cin), .nG0(n181_1_ng), .nP0(n181_1_np), .nG1(n181_2_ng), .nP1(n181_2_np), .nG2(n181_3_ng),
    .nP2(n181_3_np), .nG3(n181_4_ng), .nP3(n181_4_np), .C1(n182_1_c1), .C2(n182_1_c2), .C3(n182_1_c3));  // open: nG, nP
  _377 u_377_4 (
    .nQ0(n377_4_nq0), .nQ1(n377_4_nq1), .nQ2(n377_4_nq2), .nQ3(n377_4_nq3), .nQ4(n377_4_nq4),
    .nQ5(n377_4_nq5), .nQ6(n377_4_nq6), .nQ7(n377_4_nq7));  // open: CLK, nG, nD0, nD1, nD2, nD3, nD4, nD5, nD6, nD7
  _181 u_181_4 (
    .Cin(n182_1_c3), .M(undriven_5), .nG(n181_4_ng), .nP(n181_4_np), .C(C), .Z(Z), .S0(undriven),
    .S1(undriven_2), .S2(undriven_3), .S3(undriven_4), .nF0(n181_4_nf0), .nF1(n181_4_nf1), .nF2(n181_4_nf2),
    .nF3(nN), .nA0(n377_3_nq4), .nA1(n377_3_nq5), .nA2(n377_3_nq6), .nA3(n377_3_nq7), .nB0(n377_4_nq4),
    .nB1(n377_4_nq5), .nB2(n377_4_nq6), .nB3(n377_4_nq7));
  Pull_Resistor #(.pull(1)) pull_resistor_1 (.node(Z));
  Register register_1 (.clk(clk), .Q(nA), .nwe(nwA), .D(nData));
  Register register_2 (.clk(clk), .Q(nB), .nwe(nwB), .D(nF));
  OC_Buffer oc_buffer_1 (.ng(neF), .A(nF), .B(nData_2));
endmodule

// OCB
module OC_Buffer (
  input  [15:0] A,
  input  ng,
  output [15:0] B
);

  wire n641_1_p1, n641_1_p4, n641_1_p5, n641_1_p6, n641_1_p7, n641_1_p8, n641_1_p11, n641_1_p12, n641_1_p13,
       n641_1_p14, n641_1_p15, n641_1_p17, n641_1_p18, n641_2_p1, n641_2_p4, n641_2_p5, n641_2_p7, n641_2_p8,
       n641_2_p11, n641_2_p12, n641_2_p13, n641_2_p14, n641_2_p15, n641_2_p18;

  // _641 641_1: pin names not known; wires that end beside it: n641_1_p1, A[15:8], 1'b1, n641_1_p4, n641_1_p5, n641_1_p6, n641_1_p7, n641_1_p8, A[15:8], A[15:8], n641_1_p11, n641_1_p12, n641_1_p13, n641_1_p14, n641_1_p15, B[15:8], n641_1_p17, n641_1_p18, 1'b1
  // _641 641_2: pin names not known; wires that end beside it: n641_2_p1, A[15:8], 1'b1, n641_2_p4, n641_2_p5, B[15:8], n641_2_p7, n641_2_p8, A[15:8], A[15:8], n641_2_p11, n641_2_p12, n641_2_p13, n641_2_p14, n641_2_p15, B[15:8], B[15:8], n641_2_p18
  // Pins of 1 and 8 bits meet at A[15:8]

  assign A[7:0] = A[15:8];
  assign B[7:0] = B[15:8];
  assign ng = A[8];
endmodule

// OCT
module OC_Transceiver (
  input  [15:0] A,
  input  ng,
  input  a_b,
  input  [15:0] B,
  output [15:0] A_2,
  output [15:0] B_2
);

  wire n641_1_na0_2, n641_1_na1_2, n641_1_na2_2, n641_1_na3_2, n641_1_na7_2, n641_1_nb0_2, n641_1_nb5_2,
       n641_1_nb6_2, n641_1_nb7_2, n641_2_p1, n641_2_p8, n641_2_p11, n641_2_p12, n641_2_p13, n641_2_p14,
       n641_2_p15, n641_2_p18;

  _641 u_641_1 (
    .nG(A[8]), .nA0(n641_1_na0_2), .nA0_2(n641_1_na0_2), .nB0(n641_1_nb0_2), .nB0_2(n641_1_nb0_2),
    .nA1(n641_1_na1_2), .nA1_2(n641_1_na1_2), .nB1(A[8]), .nB1_2(A[8]), .nA2(n641_1_na2_2),
    .nA2_2(n641_1_na2_2), .nA3(n641_1_na3_2), .nA3_2(n641_1_na3_2), .nB2(a_b), .nB2_2(a_b), .nB3(a_b),
    .nB3_2(a_b), .nA4(a_b), .nA4_2(a_b), .nA5(a_b), .nA5_2(a_b), .nA6(a_b), .nA6_2(a_b),
    .nA7_2(n641_1_na7_2), .nB4(a_b), .nB4_2(a_b), .nB5(n641_1_nb5_2), .nB5_2(n641_1_nb5_2),
    .nB6(n641_1_nb6_2), .nB6_2(n641_1_nb6_2), .nB7(n641_1_nb7_2), .nB7_2(n641_1_nb7_2), .nA7(n641_1_na7_2),
    .A_B(A[8]));
  // _641 641_2: pin names not known; wires that end beside it: n641_2_p1, A[15:8], {B[15:9], a_b}, {B[15:9], a_b}, {B[15:9], a_b}, {B[15:9], a_b}, {B[15:9], a_b}, n641_2_p8, A[15:8], A_2[15:8], n641_2_p11, n641_2_p12, n641_2_p13, n641_2_p14, n641_2_p15, {B[15:9], a_b}, {B[15:9], a_b}, n641_2_p18
  // Pins of 1 and 8 bits meet at {B[15:9], a_b}
  // Pins of 1 and 8 bits meet at A[15:8]

  assign A[7:0] = A[15:8];
  assign A_2[7:0] = A[15:8];
  assign B[8:0] = {a_b, B[15:9], a_b};
  assign B_2[15:8] = {B[15:9], a_b};
  assign ng = A[8];
endmodule

// Reg
module Register (
  input  [15:0] D,
  input  clk,
  input  nwe,
  output [15:0] Q
);

  // _377 377_1: pin names not known; wires that end beside it: {D[7:1], clk}, {D[7:1], clk}, nwe, nwe, D[15:8], {D[7:1], clk}, nwe, Q[15:8]
  // _377 377_2: pin names not known; wires that end beside it: {D[7:1], clk}, {D[7:1], clk}, nwe, Q[15:8], D[15:8], D[15:8]
  // Pins of 1 and 8 bits meet at {D[7:1], clk}

  assign D[0] = clk;
  assign Q[7:0] = Q[15:8];
endmodule

// Ctr
module Counter (
  input  [15:0] P,
  input  clk,
  input  nwe,
  input  u_d,
  input  nce,
  output ntc,
  output [15:0] Q
);

  wire n169_1_p7, n169_2_p10, n169_3_p11;

  // _169 169_1: pin names not known; wires that end beside it: nce, nce, nce, clk, nwe, P[3:0], n169_1_p7, Q[3:0], clk
  // _169 169_2: pin names not known; wires that end beside it: n169_1_p7, n169_1_p7, n169_1_p7, Q[3:0], nce, clk, nwe, P[7:4], Q[15:12], n169_2_p10, n169_1_p7, Q[3:0], n169_2_p10, clk
  // _169 169_3: pin names not known; wires that end beside it: n169_2_p10, n169_1_p7, n169_1_p7, n169_1_p7, Q[3:0], n169_2_p10, clk, nwe, P[11:8], Q[15:12], n169_3_p11, n169_1_p7, Q[3:0], n169_3_p11, clk
  // _169 169_4: pin names not known; wires that end beside it: n169_3_p11, n169_1_p7, n169_1_p7, n169_1_p7, Q[3:0], n169_3_p11, clk, nwe, P[15:12], Q[15:12], ntc

  assign Q[11:4] = {Q[15:12], Q[15:12]};
  assign u_d = nwe;
endmodule

module _138 (
  input  A,
  input  B,
  input  C,
  input  G1,
  input  nG2,
  input  nG3,
  output nY0,
  output nY1,
  output nY2,
  output nY3,
  output nY4,
  output nY5,
  output nY6,
  output nY7
);

  wire and_1_out;

  and and_1 (and_1_out, G1, ~nG2, ~nG3);  // AND_Gate
  nand nand_1 (nY0, ~A, ~B, ~C, and_1_out);  // NAND_Gate
  nand nand_2 (nY1, A, ~B, ~C, and_1_out);  // NAND_Gate
  nand nand_3 (nY2, ~A, B, ~C, and_1_out);  // NAND_Gate
  nand nand_4 (nY3, A, B, ~C, and_1_out);  // NAND_Gate
  nand nand_5 (nY4, ~A, ~B, C, and_1_out);  // NAND_Gate
  nand nand_6 (nY5, A, ~B, C, and_1_out);  // NAND_Gate
  nand nand_7 (nY6, ~A, B, C, and_1_out);  // NAND_Gate
  nand nand_8 (nY7, A, B, C, and_1_out);
endmodule

module _151 (
  input  A,
  input  B,
  input  C,
  input  nG,
  input  D0,
  input  D1,
  input  D2,
  input  D3,
  input  D4,
  input  D5,
  input  D6,
  input  D7,
  output Y,
  output nY
);

  wire and_1_out, and_2_out, and_3_out, and_4_out, and_5_out, and_6_out, and_7_out, and_8_out;

  and and_1 (and_1_out, D0, ~A, ~B, ~C, ~nG);  // AND_Gate
  and and_2 (and_2_out, D1, A, ~B, ~C, ~nG);  // AND_Gate
  and and_3 (and_3_out, D2, ~A, B, ~C, ~nG);  // AND_Gate
  and and_4 (and_4_out, D3, A, B, ~C, ~nG);  // AND_Gate
  and and_5 (and_5_out, D4, ~A, ~B, C, ~nG);  // AND_Gate
  and and_6 (and_6_out, D5, A, ~B, C, ~nG);  // AND_Gate
  and and_7 (and_7_out, D6, ~A, B, C, ~nG);  // AND_Gate
  and and_8 (and_8_out, D7, A, B, C, ~nG);  // AND_Gate
  or or_1 (Y, and_1_out, and_2_out, and_3_out, and_4_out, and_5_out, and_6_out, and_7_out, and_8_out);
  not not_1 (nY, Y);
endmodule

module _153 (
  input  A,
  input  B,
  input  _1G,
  input  _1C0,
  input  _1C1,
  input  _1C2,
  input  _1C3,
  input  _2G,
  input  _2C0,
  input  _2C1,
  input  _2C2,
  input  _2C3,
  output _1Y,
  output _2Y
);

  wire and_1_out, and_2_out, and_3_out, and_4_out, and_5_out, and_6_out, and_7_out, and_8_out;

  and and_1 (and_1_out, ~_1G, ~A, ~B, _1C0);  // AND_Gate
  and and_2 (and_2_out, ~_1G, A, ~B, _1C1);  // AND_Gate
  and and_3 (and_3_out, ~_1G, ~A, B, _1C2);  // AND_Gate
  and and_4 (and_4_out, ~_1G, A, B, _1C3);  // AND_Gate
  and and_5 (and_5_out, ~_2G, ~A, ~B, _2C0);  // AND_Gate
  and and_6 (and_6_out, ~_2G, A, ~B, _2C1);  // AND_Gate
  and and_7 (and_7_out, ~_2G, ~A, B, _2C2);  // AND_Gate
  and and_8 (and_8_out, ~_2G, A, B, _2C3);  // AND_Gate
  or or_1 (_1Y, and_1_out, and_2_out, and_3_out, and_4_out);
  or or_2 (_2Y, and_5_out, and_6_out, and_7_out, and_8_out);
endmodule

module _169 (
  input  CLK,
  input  nD0,
  input  nD1,
  input  nD2,
  input  nD3,
  input  nW,
  input  D_U,
  input  nT,
  input  nP,
  output nC,
  output nQ0,
  output nQ1,
  output nQ2,
  output nQ3
);

  wire and_1_out, and_2_out, and_3_out, and_4_out, and_5_out, and_6_out, and_7_out, and_8_out, and_9_out,
       and_10_out, and_11_out, and_12_out, and_13_out, and_14_out, and_15_out, and_16_out, and_17_out,
       and_18_out, and_19_out, and_20_out, and_21_out, or_1_out, or_2_out, or_3_out, or_4_out, or_5_out,
       or_6_out, or_7_out, or_8_out, or_9_out, or_10_out;

  and and_1 (and_1_out, ~nT, ~nP);  // AND_Gate
  and and_2 (and_2_out, ~nW, nD0);  // AND_Gate
  and and_3 (and_3_out, ~nQ0, and_1_out, nW);  // AND_Gate
  or or_1 (or_1_out, and_3_out, and_2_out, and_5_out);
  or or_2 (or_2_out, ~and_1_out, ~nQ0);  // OR_Gate
  and and_4 (and_4_out, nQ0, ~nQ1, and_1_out, D_U, nW);  // AND_Gate
  and and_5 (and_5_out, nQ0, ~and_1_out, nW);  // AND_Gate
  D_Flip_Flop d_ff_1 (.clk(CLK), .D(or_1_out), .Q(nQ0));  // open: Qn, preset, en, reset
  and and_6 (and_6_out, ~nW, nD1);  // AND_Gate
  and and_7 (and_7_out, or_2_out, nQ1, D_U, nW);
  or or_3 (or_3_out, and_4_out, and_7_out, and_6_out, and_9_out, and_8_out);
  or or_4 (or_4_out, ~and_1_out, nQ0);  // OR_Gate
  and and_8 (and_8_out, or_4_out, nQ1, ~D_U, nW);  // AND_Gate
  and and_9 (and_9_out, ~nQ0, ~nQ1, and_1_out, ~D_U, nW);  // AND_Gate
  D_Flip_Flop d_ff_2 (.clk(CLK), .D(or_3_out), .Q(nQ1));  // open: Qn, preset, en, reset
  or or_5 (or_5_out, ~and_1_out, ~nQ0, ~nQ1);  // OR_Gate
  and and_10 (and_10_out, nQ0, nQ1, ~nQ2, and_1_out, D_U, nW);  // AND_Gate
  and and_11 (and_11_out, ~nW, nD2);  // AND_Gate
  and and_12 (and_12_out, or_5_out, nQ2, D_U, nW);
  or or_6 (or_6_out, and_10_out, and_12_out, and_11_out, and_13_out, and_14_out);
  or or_7 (or_7_out, ~and_1_out, nQ0, nQ1);  // OR_Gate
  and and_13 (and_13_out, ~nQ0, ~nQ1, ~nQ2, and_1_out, ~D_U, nW);  // AND_Gate
  and and_14 (and_14_out, or_7_out, nQ2, ~D_U, nW);  // AND_Gate
  D_Flip_Flop d_ff_3 (.clk(CLK), .D(or_6_out), .Q(nQ2));  // open: Qn, preset, en, reset
  or or_8 (or_8_out, ~and_1_out, ~nQ0, ~nQ1, ~nQ2);  // OR_Gate
  and and_15 (and_15_out, nQ0, nQ1, nQ2, ~nQ3, and_1_out, D_U, nW);  // AND_Gate
  and and_16 (and_16_out, ~nW, nD3);  // AND_Gate
  and and_17 (and_17_out, or_8_out, nQ3, D_U, nW);
  or or_9 (or_9_out, and_15_out, and_17_out, and_16_out, and_18_out, and_19_out);
  or or_10 (or_10_out, ~and_1_out, nQ0, nQ1, nQ2);  // OR_Gate
  and and_18 (and_18_out, ~nQ0, ~nQ1, ~nQ2, ~nQ3, and_1_out, ~D_U, nW);  // AND_Gate
  and and_19 (and_19_out, or_10_out, nQ3, ~D_U, nW);  // AND_Gate
  D_Flip_Flop d_ff_4 (.clk(CLK), .D(or_9_out), .Q(nQ3));  // open: Qn, preset, en, reset
  and and_20 (and_20_out, D_U, ~nT, nQ0, nQ1, nQ2, nQ3);  // AND_Gate
  and and_21 (and_21_out, ~D_U, ~nT, ~nQ0, ~nQ1, ~nQ2, ~nQ3);  // AND_Gate
  nor nor_1 (nC, and_20_out, and_21_out);
endmodule

module _181 (
  input  nA0,
  input  nA1,
  input  nA2,
  input  nA3,
  input  nB0,
  input  nB1,
  input  nB2,
  input  nB3,
  input  S0,
  input  S1,
  input  S2,
  input  S3,
  input  M,
  input  Cin,
  output C,
  output Z,
  output nG,
  output nP,
  output nF0,
  output nF1,
  output nF2,
  output nF3
);

  wire and_1_out, and_2_out, and_3_out, and_4_out, and_5_out, and_6_out, and_7_out, and_8_out, and_9_out,
       and_10_out, and_11_out, and_12_out, and_13_out, and_14_out, and_15_out, and_16_out, and_17_out,
       and_18_out, and_19_out, and_20_out, and_21_out, and_22_out, and_23_out, and_24_out, and_25_out,
       and_27_out, and_28_out, and_29_out, nand_1_out, nand_3_out, nor_1_out, nor_2_out, nor_3_out,
       nor_4_out, nor_5_out, nor_6_out, nor_7_out, nor_8_out, nor_9_out, nor_10_out, nor_11_out, not_1_out,
       xor_1_out, xor_3_out, xor_5_out, xor_7_out;

  not not_1 (not_1_out, M);
  nand nand_1 (nand_1_out, Cin, not_1_out);
  and and_1 (and_1_out, nB0, S0);
  and and_2 (and_2_out, nA0, ~nB0, S2);  // AND_Gate
  and and_3 (and_3_out, ~nB0, S1);  // AND_Gate
  nor nor_1 (nor_1_out, nA0, and_1_out, and_3_out);
  and and_4 (and_4_out, nor_1_out, not_1_out);
  nor nor_2 (nor_2_out, and_4_out, and_7_out);
  xor xor_1 (xor_1_out, nor_1_out, nor_3_out);
  xor xor_2 (nF0, nand_1_out, xor_1_out);
  and and_5 (and_5_out, nA0, nB0, S3);
  and and_6 (and_6_out, nB1, S0);
  nor nor_3 (nor_3_out, and_2_out, and_5_out);
  nor nor_4 (nor_4_out, nA1, and_6_out, and_11_out);
  and and_7 (and_7_out, Cin, nor_3_out, not_1_out);
  and and_8 (and_8_out, nor_4_out, not_1_out);
  xor xor_3 (xor_3_out, nor_4_out, nor_5_out);
  xor xor_4 (nF1, nor_2_out, xor_3_out);
  and and_9 (and_9_out, nA1, ~nB1, S2);  // AND_Gate
  and and_10 (and_10_out, nA1, nB1, S3);
  and and_11 (and_11_out, ~nB1, S1);  // AND_Gate
  nor nor_5 (nor_5_out, and_9_out, and_10_out);
  and and_12 (and_12_out, Cin, nor_3_out, nor_5_out, not_1_out);
  and and_13 (and_13_out, nor_1_out, nor_5_out, not_1_out);
  nor nor_6 (nor_6_out, and_8_out, and_13_out, and_12_out);
  and and_14 (and_14_out, nB2, S0);
  and and_15 (and_15_out, ~nB2, S1);  // AND_Gate
  nor nor_7 (nor_7_out, nA2, and_14_out, and_15_out);
  and and_16 (and_16_out, nor_7_out, not_1_out);
  and and_17 (and_17_out, nor_4_out, nor_8_out, not_1_out);
  xor xor_5 (xor_5_out, nor_7_out, nor_8_out);
  xor xor_6 (nF2, nor_6_out, xor_5_out);
  and and_18 (and_18_out, nA2, nB2, S3);
  and and_19 (and_19_out, nA2, ~nB2, S2);  // AND_Gate
  nor nor_8 (nor_8_out, and_19_out, and_18_out);
  and and_20 (and_20_out, nor_1_out, nor_5_out, nor_8_out, not_1_out);
  nor nor_9 (nor_9_out, and_16_out, and_17_out, and_20_out, and_24_out);
  and and_21 (and_21_out, nB3, S0);
  and and_22 (and_22_out, nA3, ~nB3, S2);  // AND_Gate
  and and_23 (and_23_out, ~nB3, S1);  // AND_Gate
  nor nor_10 (nor_10_out, nA3, and_21_out, and_23_out);
  nor nor_11 (nor_11_out, and_22_out, and_25_out);
  and and_24 (and_24_out, Cin, nor_3_out, nor_5_out, nor_8_out, not_1_out);
  xor xor_7 (xor_7_out, nor_10_out, nor_11_out);
  xor xor_8 (nF3, nor_9_out, xor_7_out);
  and and_25 (and_25_out, nA3, nB3, S3);
  nand nand_2 (nP, nor_3_out, nor_5_out, nor_8_out, nor_11_out);
  nand nand_3 (nand_3_out, Cin, nor_3_out, nor_5_out, nor_8_out, nor_11_out);
  and and_26 (Z, nF0, nF1, nF2, nF3);
  and and_27 (and_27_out, nor_1_out, nor_5_out, nor_8_out, nor_11_out);
  and and_28 (and_28_out, nor_4_out, nor_8_out, nor_11_out);
  nor nor_12 (nG, and_27_out, and_28_out, and_29_out, nor_10_out);
  and and_29 (and_29_out, nor_7_out, nor_11_out);
  or or_1 (C, ~nand_3_out, ~nG);  // OR_Gate

  // Notes on the sheet:
  //   and_26 drives only 0 and floats otherwise
endmodule

module _182 (
  input  nG0,
  input  nP0,
  input  nG1,
  input  nP1,
  input  nG2,
  input  nP2,
  input  nG3,
  input  nP3,
  input  Cin,
  output C1,
  output C2,
  output C3,
  output nG,
  output nP
);

  wire and_1_out, and_2_out, and_3_out, and_4_out, and_5_out, and_6_out, and_7_out, and_8_out, and_9_out,
       and_10_out, and_11_out, and_12_out, and_13_out;

  and and_1 (and_1_out, nG0, nP0);
  nor nor_1 (C1, and_1_out, and_2_out);
  and and_2 (and_2_out, nG0, ~Cin);  // AND_Gate
  and and_3 (and_3_out, nG1, nP1);
  and and_4 (and_4_out, nG0, nG1, ~Cin);  // AND_Gate
  and and_5 (and_5_out, nG2, nP2);
  and and_6 (and_6_out, nG0, nP0, nG1);
  nor nor_2 (C2, and_3_out, and_6_out, and_4_out);
  and and_7 (and_7_out, nG0, nP0, nG1, nG2);
  and and_8 (and_8_out, nG1, nP1, nG2);
  nor nor_3 (C3, and_5_out, and_8_out, and_7_out, and_9_out);
  and and_9 (and_9_out, nG0, nG1, nG2, ~Cin);  // AND_Gate
  and and_10 (and_10_out, nG3, nP3);
  and and_11 (and_11_out, nG2, nP2, nG3);
  and and_12 (and_12_out, nG1, nP1, nG2, nG3);
  or or_1 (nG, and_10_out, and_11_out, and_12_out, and_13_out);
  and and_13 (and_13_out, nG0, nG1, nG2, nG3);
  or or_2 (nP, nP0, nP1, nP2, nP3);
endmodule

module _377 (
  input  nD0,
  input  nD1,
  input  nD2,
  input  nD3,
  input  nD4,
  input  nD5,
  input  nD6,
  input  nD7,
  input  CLK,
  input  nG,
  output nQ0,
  output nQ1,
  output nQ2,
  output nQ3,
  output nQ4,
  output nQ5,
  output nQ6,
  output nQ7
);

  wire and_1_out, and_2_out, d_ff_1_q, d_ff_2_q, d_ff_3_q, d_ff_4_q, d_ff_5_q, d_ff_6_q, d_ff_7_q, d_ff_8_q,
       not_1_out, not_2_out, not_4_out, not_6_out, not_8_out, not_10_out, not_12_out, not_14_out;

  and and_1 (and_1_out, CLK, ~and_2_out);  // AND_Gate
  not not_1 (not_1_out, nD0);
  and and_2 (and_2_out, ~and_1_out, ~nG);  // AND_Gate
  D_Flip_Flop d_ff_1 (.clk(CLK), .D(not_1_out), .Q(d_ff_1_q), .en(and_2_out));  // open: Qn, preset, reset
  not not_2 (not_2_out, nD1);
  not not_3 (nQ0, d_ff_1_q);
  D_Flip_Flop d_ff_2 (.clk(CLK), .D(not_2_out), .Q(d_ff_2_q), .en(and_2_out));  // open: Qn, preset, reset
  not not_4 (not_4_out, nD2);
  not not_5 (nQ1, d_ff_2_q);
  D_Flip_Flop d_ff_3 (.clk(CLK), .D(not_4_out), .Q(d_ff_3_q), .en(and_2_out));  // open: Qn, preset, reset
  not not_6 (not_6_out, nD3);
  not not_7 (nQ2, d_ff_3_q);
  D_Flip_Flop d_ff_4 (.clk(CLK), .D(not_6_out), .Q(d_ff_4_q), .en(and_2_out));  // open: Qn, preset, reset
  not not_8 (not_8_out, nD4);
  not not_9 (nQ3, d_ff_4_q);
  D_Flip_Flop d_ff_5 (.clk(CLK), .D(not_8_out), .Q(d_ff_5_q), .en(and_2_out));  // open: Qn, preset, reset
  not not_10 (not_10_out, nD5);
  not not_11 (nQ4, d_ff_5_q);
  D_Flip_Flop d_ff_6 (.clk(CLK), .D(not_10_out), .Q(d_ff_6_q), .en(and_2_out));  // open: Qn, preset, reset
  not not_12 (not_12_out, nD6);
  not not_13 (nQ5, d_ff_6_q);
  D_Flip_Flop d_ff_7 (.clk(CLK), .D(not_12_out), .Q(d_ff_7_q), .en(and_2_out));  // open: Qn, preset, reset
  not not_14 (not_14_out, nD7);
  not not_15 (nQ6, d_ff_7_q);
  D_Flip_Flop d_ff_8 (.clk(CLK), .D(not_14_out), .Q(d_ff_8_q), .en(and_2_out));  // open: Qn, preset, reset
  not not_16 (nQ7, d_ff_8_q);
endmodule

module _641 (
  input  nA0,
  input  nA1,
  input  nA2,
  input  nA3,
  input  nA4,
  input  nA5,
  input  nA6,
  input  nA7,
  input  nG,
  input  A_B,
  input  nB0,
  input  nB1,
  input  nB2,
  input  nB3,
  input  nB4,
  input  nB5,
  input  nB6,
  input  nB7,
  output nA0_2,
  output nA1_2,
  output nA2_2,
  output nA3_2,
  output nA4_2,
  output nA5_2,
  output nA6_2,
  output nA7_2,
  output nB0_2,
  output nB1_2,
  output nB2_2,
  output nB3_2,
  output nB4_2,
  output nB5_2,
  output nB6_2,
  output nB7_2
);

  wire and_1_out, and_2_out;

  and and_1 (and_1_out, A_B, ~nG);  // AND_Gate
  nand nand_1 (nA0_2, ~nB0, and_2_out);  // NAND_Gate
  nand nand_2 (nB0_2, and_1_out, ~nA0);  // NAND_Gate
  and and_2 (and_2_out, ~A_B, ~nG);  // AND_Gate
  nand nand_3 (nA1_2, ~nB1, and_2_out);  // NAND_Gate
  nand nand_4 (nB2_2, and_1_out, ~nA2);  // NAND_Gate
  nand nand_5 (nB1_2, and_1_out, ~nA1);  // NAND_Gate
  nand nand_6 (nA2_2, ~nB2, and_2_out);  // NAND_Gate
  nand nand_7 (nB3_2, and_1_out, ~nA3);  // NAND_Gate
  nand nand_8 (nA4_2, ~nB4, and_2_out);  // NAND_Gate
  nand nand_9 (nA3_2, ~nB3, and_2_out);  // NAND_Gate
  nand nand_10 (nB4_2, and_1_out, ~nA4);  // NAND_Gate
  nand nand_11 (nA5_2, ~nB5, and_2_out);  // NAND_Gate
  nand nand_12 (nB6_2, and_1_out, ~nA6);  // NAND_Gate
  nand nand_13 (nB5_2, and_1_out, ~nA5);  // NAND_Gate
  nand nand_14 (nA6_2, ~nB6, and_2_out);  // NAND_Gate
  nand nand_15 (nB7_2, and_1_out, ~nA7);  // NAND_Gate
  nand nand_16 (nA7_2, ~nB7, and_2_out);  // NAND_Gate

  // Notes on the sheet:
  //   nand_1 drives only 0 and floats otherwise
  //   nand_2 drives only 0 and floats otherwise
  //   nand_3 drives only 0 and floats otherwise
  //   nand_4 drives only 0 and floats otherwise
  //   nand_5 drives only 0 and floats otherwise
  //   nand_6 drives only 0 and floats otherwise
  //   nand_7 drives only 0 and floats otherwise
  //   nand_8 drives only 0 and floats otherwise
  //   nand_9 drives only 0 and floats otherwise
  //   nand_10 drives only 0 and floats otherwise
  //   nand_11 drives only 0 and floats otherwise
  //   nand_12 drives only 0 and floats otherwise
  //   nand_13 drives only 0 and floats otherwise
  //   nand_14 drives only 0 and floats otherwise
  //   nand_15 drives only 0 and floats otherwise
  //   nand_16 drives only 0 and floats otherwise
endmodule

module _62256 (
  input  nD0i,
  input  nD1i,
  input  nD2i,
  input  nD3i,
  input  nD4i,
  input  nD5i,
  input  nD6i,
  input  nD7i,
  input  CLK,
  input  nG,
  input  nR,
  input  nW,
  input  nA0,
  input  nA1,
  input  nA2,
  input  nA3,
  input  nA4,
  input  nA5,
  input  nA6,
  input  nA7,
  input  nA8,
  input  nA9,
  input  nAa,
  input  nAb,
  input  nAc,
  input  nAd,
  input  nAe,
  output nD0o,
  output nD1o,
  output nD2o,
  output nD3o,
  output nD4o,
  output nD5o,
  output nD6o,
  output nD7o
);

  wire and_1_out, and_2_out, not_2_out;
  wire [7:0] ram_1_data;
  wire [14:0] not_1_out;

  assign not_1_out = ~{nAe, nAd, nAc, nAb, nAa, nA9, nA8, nA7, nA6, nA5, nA4, nA3, nA2, nA1, nA0};  // NOT_Gate not_1, 15 bits wide
  and and_1 (and_1_out, ~nG, nW, ~nR);  // AND_Gate
  and and_2 (and_2_out, ~nG, ~nW);  // AND_Gate
  RAM #(.addrWidth(15)) ram_1 (
    .addr(not_1_out), .data(ram_1_data), .clk(CLK), .ld(not_2_out), .clr(1'b0));  // open: sel
  not not_2 (not_2_out, and_2_out);
  assign ram_1_data = and_2_out ? ~{nD7i, nD6i, nD5i, nD4i, nD3i, nD2i, nD1i, nD0i} : 8'bz;  // Controlled_Inverter controlled_inverter_1
  assign {nD7o, nD6o, nD5o, nD4o, nD3o, nD2o, nD1o, nD0o} = and_1_out ? ~ram_1_data : 8'bz;  // Controlled_Inverter controlled_inverter_2
endmodule
