// Logisim project CPU-old.circ as structural Verilog: 22 circuits, main circuit CPU
module CPU (
  input  run,
  input  [15:0] S
);

  wire al_out, alu_board_1_p11, alu_board_1_p12, alu_board_1_p13, clock_1_out, control_board_1_p15,
       control_board_1_p17, control_board_1_p18, control_board_1_p19, dep_out, exam_out, not_3_out,
       not_5_out, not_6_out, not_7_out, not_10_out, not_12_out, not_14_out, not_15_out, ram_board_1_p2,
       ram_board_1_p3, ram_board_1_p9, ram_board_1_p10, step_out;
  wire [6:0] control_board_1_p14, not_13_out;
  wire [7:0] control_board_1_p16;
  wire [15:0] alu_board_1_p8, alu_board_1_p9, alu_board_1_p10, not_1_out, not_2_out, not_4_out, not_8_out,
       not_9_out, not_11_out, not_16_out, not_17_out, not_18_out, pull_resistor_1_node, pull_resistor_2_node,
       register_board_1_na, register_board_1_nd, register_board_1_np;

  Pull_Resistor #(.pull(1)) pull_resistor_1 (.node(pull_resistor_1_node));
  Clock clock_1 (.out(clock_1_out));
  assign not_1_out = ~pull_resistor_1_node;  // NOT_Gate not_1, 16 bits wide
  // Probe on not_1_out
  Pull_Resistor #(.pull(1)) pull_resistor_2 (.node(pull_resistor_2_node));
  assign not_2_out = ~pull_resistor_2_node;  // NOT_Gate not_2, 16 bits wide
  // Probe on not_2_out
  // RAM_Board ram_board_1: pin names not known; wires that end beside it: clock_1_out, ram_board_1_p2, ram_board_1_p3, ram_board_1_p2, ram_board_1_p3, pull_resistor_2_node, pull_resistor_1_node, pull_resistor_1_node, ram_board_1_p9, ram_board_1_p10
  not not_3 (not_3_out, run);
  // ALU_Board alu_board_1: pin names not known; wires that end beside it: clock_1_out, ram_board_1_p10, ram_board_1_p3, ram_board_1_p2, pull_resistor_2_node, pull_resistor_1_node, pull_resistor_1_node, alu_board_1_p8, alu_board_1_p9, alu_board_1_p10, alu_board_1_p11, alu_board_1_p12, alu_board_1_p13, ram_board_1_p2
  assign not_4_out = ~alu_board_1_p8;  // NOT_Gate not_4, 16 bits wide
  // Probe on not_4_out
  Button step (.out(step_out));
  Button exam (.out(exam_out));
  Button al (.out(al_out));
  not not_5 (not_5_out, exam_out);
  not not_6 (not_6_out, step_out);
  not not_7 (not_7_out, al_out);
  assign not_8_out = ~alu_board_1_p9;  // NOT_Gate not_8, 16 bits wide
  assign not_9_out = ~alu_board_1_p10;  // NOT_Gate not_9, 16 bits wide
  // Probe on not_9_out
  // Probe on not_8_out
  Button dep (.out(dep_out));
  not not_10 (not_10_out, dep_out);
  // Control_Board control_board_1: pin names not known; wires that end beside it: clock_1_out, ram_board_1_p9, not_3_out, not_6_out, not_7_out, not_5_out, not_10_out, alu_board_1_p11, alu_board_1_p12, alu_board_1_p13, ram_board_1_p2, ram_board_1_p3, pull_resistor_2_node, control_board_1_p14, control_board_1_p15, control_board_1_p16, control_board_1_p17, control_board_1_p18, control_board_1_p19, ram_board_1_p2, ram_board_1_p3, ram_board_1_p2, ram_board_1_p3, ram_board_1_p2
  assign not_11_out = ~S;  // NOT_Gate not_11, 16 bits wide
  OC_Buffer oc_buffer_1 (.ng(control_board_1_p15), .In(not_11_out), .Out(pull_resistor_1_node));
  not not_12 (not_12_out, control_board_1_p18);
  assign not_13_out = ~control_board_1_p14;  // NOT_Gate not_13, 7 bits wide
  not not_14 (not_14_out, control_board_1_p17);
  // Probe on not_13_out
  // Probe on not_12_out
  // Probe on not_14_out
  Register_Board register_board_1 (
    .clk(clock_1_out), .nD(register_board_1_nd), .nA(register_board_1_na), .nP(register_board_1_np),
    .nData(pull_resistor_1_node), .nData_2(pull_resistor_1_node), .nAddress(pull_resistor_2_node),
    .nControl(control_board_1_p16));
  not not_15 (not_15_out, control_board_1_p19);
  // Probe on not_15_out
  assign not_16_out = ~register_board_1_nd;  // NOT_Gate not_16, 16 bits wide
  assign not_17_out = ~register_board_1_na;  // NOT_Gate not_17, 16 bits wide
  // Probe on not_16_out
  // Probe on not_17_out
  assign not_18_out = ~register_board_1_np;  // NOT_Gate not_18, 16 bits wide
  // Probe on not_18_out
endmodule

module Front_Board (
  input  [7:0] nDL,
  input  [7:0] nDH,
  input  [7:0] in_3,
  input  [7:0] in_4,
  input  [7:0] in_5,
  input  [7:0] in_6,
  input  [7:0] nAL,
  input  [7:0] nAH,
  input  [7:0] in_9,
  input  [7:0] in_10,
  input  nrun,
  input  nstep,
  input  naddr,
  input  [15:0] nS,
  input  nexam,
  input  ndep,
  output [15:0] nD,
  output [15:0] nA,
  output [7:0] nDL_2,
  output [7:0] nDH_2,
  output [7:0] out_21,
  output [7:0] out_22,
  output [7:0] out_23,
  output [7:0] nAL_2,
  output [7:0] nAH_2,
  output [7:0] out_26
);

  wire clk;

  _377 u_377_1 (.clk(clk), .ng(in_5[0]), .D(nS[7:0]), .Q(nDL_2));
  _377 u_377_2 (.clk(clk), .ng(in_5[0]), .D(nS[15:8]), .Q(nDH_2));
  _279_1 u_279_1_1 (.q(out_23[1]));  // open: nr, ns1, ns2
  _279_2 u_279_2_1 (.q(out_23[2]));  // open: nr, ns
  _279_1 u_279_1_2 (.q(out_23[3]));  // open: nr, ns1, ns2
  _279_2 u_279_2_2 (.q(out_23[4]));  // open: nr, ns

  assign in_10[7:5] = in_4[7:5];
  assign nA = {nAH, nAL};
  assign nD = {nDH, nDL};

  // Other names for the same wires on the sheet: nsd = in_5[0]; gnd = in_4[5]; v_plus = in_4[6]; led_plus = in_4[7]
endmodule

module Control_Board (
  input  clk,
  input  ng,
  input  nrun,
  input  nstep,
  input  clk_2,
  input  naddr,
  input  ng_2,
  input  nexam,
  input  nread,
  input  ndep,
  input  nwrite,
  input  c,
  input  c_2,
  input  z,
  input  nn,
  input  [15:0] nAddress,
  input  nr,
  input  nr_2,
  input  nw,
  input  nw_2,
  input  [7:0] nAL,
  input  [7:0] nAH,
  output nsd,
  output nfd,
  output nda,
  output ndb,
  output [7:0] nControl,
  output [3:0] S,
  output m,
  output cin,
  output nc,
  output nz,
  output nn_2,
  output [6:0] nState,
  output [7:0] nAL_2,
  output [7:0] nAH_2
);

  wire _04_3_out, _11_out, _32_11_out, _32_out, _40_out, n151_1_ny;
  wire [7:0] _32_5_out, n377_3_q;
  wire [7:4] n377_2_q;
  wire [7:7] n377_1_q;

  not _04 (nc, c);
  not _04_2 (nz, z);
  not _04_3 (_04_3_out, nn);
  _151 u_151_1 (
    .a(nAL[0]), .b(nAL[1]), .c(nAL[2]), .ng(ng), .d0(nn), .d1(_04_3_out), .d2(nz), .d3(z), .d4(nc), .d5(c),
    .d6(1'b1), .d7(1'b0), .ny(n151_1_ny));  // open: y
  _377 u_377_1 (
    .clk(clk), .ng(1'b0), .D({_32_5_out[7:4], nState[4], nState[5], nState[6], _32_5_out[0]}),
    .Q({n377_1_q[7], nState[0], nState[1], nState[2], nControl[1], nState[4], nState[5], nState[6]}));
  nand _40 (_40_out, nState[6], nState[5], nState[4]);
  or _32 (_32_out, n377_1_q[7], nstep);
  or _32_2 (_32_5_out[4], n377_1_q[7], naddr);
  or _32_3 (_32_5_out[5], n377_1_q[7], nexam);
  or _32_4 (_32_5_out[6], n377_1_q[7], ndep);
  nand _40_2 (_32_5_out[7], nstep, naddr, nexam, ndep);
  or _32_5 (_32_5_out[0], _40_out, _11_out);
  and _11 (_11_out, nrun, _32_out);
  and _21 (nr, nState[6], nState[5], nState[4], nState[1]);
  and _21_2 (nw, nControl[1], nState[0], 1'b1, 1'b1);
  and _08 (nsd, nState[2], nState[0]);
  and _08_2 (nControl[0], nState[5], nState[1]);
  and _11_2 (nControl[2], nState[6], nState[4], nState[2]);
  and _08_3 (nControl[3], nState[1], nState[0]);
  and _11_3 (nControl[4], nState[1], nState[5], nw);
  or _32_6 (nControl[5], nw, n151_1_ny);
  and _08_4 (nControl[6], nState[4], nState[6]);
  or _32_7 (nControl[7], n151_1_ny, nr);
  or _32_8 (nfd, ng_2, nread);
  or _32_9 (nda, ng_2, nwrite);
  or _32_10 (ndb, nda, nAddress[6]);
  or _32_11 (_32_11_out, nda, nAddress[7]);
  _377 u_377_2 (.clk(clk_2), .ng(nda), .D({2'b00, nAddress[5:0]}), .Q({n377_2_q, S}));
  _377 u_377_3 (.clk(clk_2), .ng(_32_11_out), .D({{7{1'b0}}, c_2}), .Q(n377_3_q));
  _153 u_153_1 (
    .a(n377_2_q[4]), .b(n377_2_q[5]), ._1g(1'b0), ._1c0(1'b0), ._1c1(1'b0), ._1c2(1'b0), ._1c3(1'b1),
    ._2g(1'b0), ._2c0(1'b1), ._2c1(1'b0), ._2c2(n377_3_q[0]), ._2c3(1'b0), ._1y(m), ._2y(cin));

  assign nAH_2 = nAH;
  assign nAL_2 = nAL;
  assign nn_2 = nn;
  assign nr_2 = nr;
  assign nState[3] = nControl[1];
  assign nw_2 = nw;
endmodule

// Reg Board
module Register_Board (
  input  [15:0] nData,
  input  clk,
  input  [7:0] nControl,
  output [15:0] nData_2,
  output [15:0] nD,
  output [15:0] nA,
  output [15:0] nP,
  output [15:0] nAddress
);

  Register register_1 (.clk(clk), .Out(nD), .nwe(nControl[0]), .In(nData));
  OC_Buffer oc_buffer_1 (.ng(nControl[1]), .In(nD), .Out(nData_2));
  Counter counter_1 (.nwe(nControl[2]), .nce(nControl[3]), .u_d(1'b0), .clk(clk), .Out(nA), .In(nData));  // open: ntc
  OC_Buffer oc_buffer_2 (.ng(nControl[4]), .In(nA), .Out(nAddress));
  Counter counter_2 (.nwe(nControl[5]), .nce(nControl[6]), .u_d(1'b0), .clk(clk), .Out(nP), .In(nData));  // open: ntc
  OC_Buffer oc_buffer_3 (.ng(nControl[6]), .In(nP), .Out(nAddress));
  OC_Buffer oc_buffer_4 (.ng(nControl[7]), .In(nP), .Out(nData_2));
endmodule

module ALU_Board (
  input  clk,
  input  [15:0] nData,
  input  nfd,
  input  nda,
  input  ndb,
  input  [3:0] S,
  input  m,
  input  cin,
  output [15:0] nData_2,
  output [15:0] nA,
  output [15:0] nB,
  output [15:0] nF,
  output c,
  output z,
  output nn
);

  Register register_1 (.clk(clk), .Out(nB), .nwe(ndb), .In(nF));
  Register register_2 (.clk(clk), .Out(nA), .nwe(nda), .In(nData));
  ALU alu_1 (.S(S), .m(m), .cout(c), .zero(z), .nA(nA), .nB(nB), .nF(nF), .cin(cin));
  OC_Buffer oc_buffer_1 (.ng(nfd), .In(nF), .Out(nData_2));

  assign nn = nF[15];
endmodule

module RAM_Board (
  input  [7:0] nDL,
  input  [7:0] nDH,
  input  clk,
  input  clk_2,
  input  nr,
  input  nr_2,
  input  nw,
  input  nw_2,
  input  [7:0] nAL,
  input  [7:0] nAH,
  output [7:0] nDL_2,
  output [7:0] nDH_2,
  output _0xxx,
  output _1xxx,
  output _2xxx,
  output _3xxx,
  output _4xxx,
  output _5xxx,
  output _6xxx,
  output _7xxx,
  output [7:0] nAL_2,
  output [7:0] nAH_2
);

  wire n153_1__1y, n153_1__2y;
  wire [7:0] n641_1_b_2, n641_2_b_2;

  _153 u_153_1 (
    .a(nr), .b(nw), ._1g(1'b0), ._1c0(1'b1), ._1c1(1'b1), ._1c2(nAH[7]), ._1c3(1'b1), ._2g(1'b0),
    ._2c0(nAH[7]), ._2c1(nAH[7]), ._2c2(nAH[7]), ._2c3(1'b1), ._1y(n153_1__1y), ._2y(n153_1__2y));
  _641 u_641_1 (.a_b(n153_1__1y), .ng(n153_1__2y), .A(nDL), .B(n641_1_b_2), .A_2(nDL), .B_2(n641_1_b_2));
  Pull_Resistor #(.pull(1)) pull_resistor_1 (.node(n641_1_b_2));
  _62256 u_62256_1 (.clk(clk), .ncs(nAH[7]), .nwe(nw), .noe(nr), .D(n641_1_b_2), .D_2(n641_1_b_2), .A({nAH[6:0], nAL}));
  _641 u_641_2 (.a_b(n153_1__1y), .ng(n153_1__2y), .A(nDH), .B(n641_2_b_2), .A_2(nDH), .B_2(n641_2_b_2));
  _62256 u_62256_2 (.clk(clk), .ncs(nAH[7]), .nwe(nw), .noe(nr), .D(n641_2_b_2), .D_2(n641_2_b_2), .A({nAH[6:0], nAL}));
  Pull_Resistor #(.pull(1)) pull_resistor_2 (.node(n641_2_b_2));
  _138 u_138_1 (
    .a(nAH[4]), .b(nAH[5]), .c(nAH[6]), .g1(nAH[7]), .ng2a(1'b0), .ng2b(1'b0), .ny0(_7xxx), .ny1(_6xxx),
    .ny2(_5xxx), .ny3(_4xxx), .ny4(_3xxx), .ny5(_2xxx), .ny6(_1xxx), .ny7(_0xxx));

  assign clk_2 = clk;
  assign nAH_2 = nAH;
  assign nAL_2 = nAL;
  assign nDH_2 = nDH;
  assign nDL_2 = nDL;
  assign nr_2 = nr;
  assign nw_2 = nw;
endmodule

// OCB
module OC_Buffer (
  input  [15:0] In,
  input  ng,
  output [15:0] Out
);

  _641 u_641_1 (.a_b(1'b1), .ng(ng), .A(In[7:0]), .B(Out[7:0]), .A_2(In[7:0]), .B_2(Out[7:0]));
  _641 u_641_2 (.a_b(1'b1), .ng(ng), .A(In[15:8]), .B(Out[15:8]), .A_2(In[15:8]), .B_2(Out[15:8]));
endmodule

// Reg
module Register (
  input  [15:0] In,
  input  clk,
  input  nwe,
  output [15:0] Out
);

  _377 u_377_1 (.clk(clk), .ng(nwe), .D(In[7:0]), .Q(Out[7:0]));
  _377 u_377_2 (.clk(clk), .ng(nwe), .D(In[15:8]), .Q(Out[15:8]));
endmodule

// Ctr
module Counter (
  input  [15:0] In,
  input  clk,
  input  nwe,
  input  u_d,
  input  nce,
  output ntc,
  output [15:0] Out
);

  wire n169_1_ntc, n169_2_ntc, n169_3_ntc;

  _169 u_169_1 (.clk(clk), .npe(nwe), .u_d(u_d), .ncet(nce), .ncep(nce), .ntc(n169_1_ntc), .P(In[3:0]), .Q(Out[3:0]));
  _169 u_169_2 (
    .clk(clk), .npe(nwe), .u_d(u_d), .ncet(nce), .ncep(n169_1_ntc), .ntc(n169_2_ntc), .P(In[7:4]),
    .Q(Out[7:4]));
  _169 u_169_3 (
    .clk(clk), .npe(nwe), .u_d(u_d), .ncet(n169_2_ntc), .ncep(n169_1_ntc), .ntc(n169_3_ntc), .P(In[11:8]),
    .Q(Out[11:8]));
  _169 u_169_4 (
    .clk(clk), .npe(nwe), .u_d(u_d), .ncet(n169_3_ntc), .ncep(n169_1_ntc), .ntc(ntc), .P(In[15:12]),
    .Q(Out[15:12]));
endmodule

module ALU (
  input  [15:0] nA,
  input  [15:0] nB,
  input  [3:0] S,
  input  m,
  input  cin,
  output zero,
  output cout,
  output [15:0] nF
);

  wire n181_1_ng, n181_1_np, n181_2_ng, n181_2_np, n181_3_ng, n181_3_np, n181_4_ng, n181_4_np, n182_1_cn_x,
       n182_1_cn_y, n182_1_cn_z;

  _181 u_181_1 (
    .S(S), .cn(cin), .m(m), .ng(n181_1_ng), .np(n181_1_np), .zero(zero), .nA(nA[3:0]), .nB(nB[3:0]),
    .nF(nF[3:0]));  // open: cn_4
  _181 u_181_2 (
    .S(S), .cn(n182_1_cn_x), .m(m), .ng(n181_2_ng), .np(n181_2_np), .zero(zero), .nA(nA[7:4]), .nB(nB[7:4]),
    .nF(nF[7:4]));  // open: cn_4
  _181 u_181_3 (
    .S(S), .cn(n182_1_cn_y), .m(m), .ng(n181_3_ng), .np(n181_3_np), .zero(zero), .nA(nA[11:8]),
    .nB(nB[11:8]), .nF(nF[11:8]));  // open: cn_4
  _182 u_182_1 (
    .cn(cin), .ng0(n181_1_ng), .np0(n181_1_np), .ng1(n181_2_ng), .np1(n181_2_np), .ng2(n181_3_ng),
    .np2(n181_3_np), .ng3(n181_4_ng), .np3(n181_4_np), .cn_x(n182_1_cn_x), .cn_y(n182_1_cn_y),
    .cn_z(n182_1_cn_z));  // open: ng, np
  _181 u_181_4 (
    .S(S), .cn(n182_1_cn_z), .m(m), .ng(n181_4_ng), .np(n181_4_np), .cn_4(cout), .zero(zero), .nA(nA[15:12]),
    .nB(nB[15:12]), .nF(nF[15:12]));
  Pull_Resistor #(.pull(1)) pull_resistor_1 (.node(zero));
endmodule

module _138 (
  input  a,
  input  b,
  input  c,
  input  g1,
  input  ng2a,
  input  ng2b,
  output ny0,
  output ny1,
  output ny2,
  output ny3,
  output ny4,
  output ny5,
  output ny6,
  output ny7
);

  wire and_1_out;

  and and_1 (and_1_out, g1, ~ng2a, ~ng2b);  // AND_Gate
  nand nand_1 (ny0, ~a, ~b, ~c, and_1_out);  // NAND_Gate
  nand nand_2 (ny1, a, ~b, ~c, and_1_out);  // NAND_Gate
  nand nand_3 (ny2, ~a, b, ~c, and_1_out);  // NAND_Gate
  nand nand_4 (ny3, a, b, ~c, and_1_out);  // NAND_Gate
  nand nand_5 (ny4, ~a, ~b, c, and_1_out);  // NAND_Gate
  nand nand_6 (ny5, a, ~b, c, and_1_out);  // NAND_Gate
  nand nand_7 (ny6, ~a, b, c, and_1_out);  // NAND_Gate
  nand nand_8 (ny7, a, b, c, and_1_out);
endmodule

module _151 (
  input  a,
  input  b,
  input  c,
  input  ng,
  input  d0,
  input  d1,
  input  d2,
  input  d3,
  input  d4,
  input  d5,
  input  d6,
  input  d7,
  output y,
  output ny
);

  wire and_1_out, and_2_out, and_3_out, and_4_out, and_5_out, and_6_out, and_7_out, and_8_out;

  and and_1 (and_1_out, d0, ~a, ~b, ~c, ~ng);  // AND_Gate
  and and_2 (and_2_out, d1, a, ~b, ~c, ~ng);  // AND_Gate
  and and_3 (and_3_out, d2, ~a, b, ~c, ~ng);  // AND_Gate
  and and_4 (and_4_out, d3, a, b, ~c, ~ng);  // AND_Gate
  and and_5 (and_5_out, d4, ~a, ~b, c, ~ng);  // AND_Gate
  and and_6 (and_6_out, d5, a, ~b, c, ~ng);  // AND_Gate
  and and_7 (and_7_out, d6, ~a, b, c, ~ng);  // AND_Gate
  and and_8 (and_8_out, d7, a, b, c, ~ng);  // AND_Gate
  or or_1 (y, and_1_out, and_2_out, and_3_out, and_4_out, and_5_out, and_6_out, and_7_out, and_8_out);
  not not_1 (ny, y);
endmodule

module _153 (
  input  a,
  input  b,
  input  _1g,
  input  _1c0,
  input  _1c1,
  input  _1c2,
  input  _1c3,
  input  _2g,
  input  _2c0,
  input  _2c1,
  input  _2c2,
  input  _2c3,
  output _1y,
  output _2y
);

  wire and_1_out, and_2_out, and_3_out, and_4_out, and_5_out, and_6_out, and_7_out, and_8_out;

  and and_1 (and_1_out, ~_1g, ~a, ~b, _1c0);  // AND_Gate
  and and_2 (and_2_out, ~_1g, a, ~b, _1c1);  // AND_Gate
  and and_3 (and_3_out, ~_1g, ~a, b, _1c2);  // AND_Gate
  and and_4 (and_4_out, ~_1g, a, b, _1c3);  // AND_Gate
  and and_5 (and_5_out, ~_2g, ~a, ~b, _2c0);  // AND_Gate
  and and_6 (and_6_out, ~_2g, a, ~b, _2c1);  // AND_Gate
  and and_7 (and_7_out, ~_2g, ~a, b, _2c2);  // AND_Gate
  and and_8 (and_8_out, ~_2g, a, b, _2c3);  // AND_Gate
  or or_1 (_1y, and_1_out, and_2_out, and_3_out, and_4_out);
  or or_2 (_2y, and_5_out, and_6_out, and_7_out, and_8_out);
endmodule

module _169 (
  input  [3:0] P,
  input  clk,
  input  npe,
  input  u_d,
  input  ncet,
  input  ncep,
  output ntc,
  output [3:0] Q
);

  wire and_1_out, and_2_out, and_3_out, and_4_out, and_5_out, and_6_out, and_7_out, and_8_out, and_9_out,
       and_10_out, and_11_out, and_12_out, and_13_out, and_14_out, and_15_out, and_16_out, and_17_out,
       and_18_out, and_19_out, and_20_out, and_21_out, or_1_out, or_2_out, or_3_out, or_4_out, or_5_out,
       or_6_out, or_7_out, or_8_out, or_9_out, or_10_out;

  and and_1 (and_1_out, ~ncet, ~ncep);  // AND_Gate
  and and_2 (and_2_out, ~npe, P[0]);  // AND_Gate
  and and_3 (and_3_out, ~Q[0], and_1_out, npe);  // AND_Gate
  or or_1 (or_1_out, and_3_out, and_2_out, and_4_out);
  and and_4 (and_4_out, Q[0], ~and_1_out, npe);  // AND_Gate
  and and_5 (and_5_out, Q[0], ~Q[1], and_1_out, u_d, npe);  // AND_Gate
  D_Flip_Flop d_ff_1 (.clk(clk), .D(or_1_out), .Q(Q[0]));  // open: Qn, preset, en, reset
  and and_6 (and_6_out, ~npe, P[1]);  // AND_Gate
  or or_2 (or_2_out, ~and_1_out, ~Q[0]);  // OR_Gate
  and and_7 (and_7_out, or_2_out, Q[1], u_d, npe);
  or or_3 (or_3_out, and_5_out, and_7_out, and_6_out, and_8_out, and_9_out);
  or or_4 (or_4_out, ~and_1_out, Q[0]);  // OR_Gate
  and and_8 (and_8_out, ~Q[0], ~Q[1], and_1_out, ~u_d, npe);  // AND_Gate
  D_Flip_Flop d_ff_2 (.clk(clk), .D(or_3_out), .Q(Q[1]));  // open: Qn, preset, en, reset
  and and_9 (and_9_out, or_4_out, Q[1], ~u_d, npe);  // AND_Gate
  and and_10 (and_10_out, Q[0], Q[1], ~Q[2], and_1_out, u_d, npe);  // AND_Gate
  or or_5 (or_5_out, ~and_1_out, ~Q[0], ~Q[1]);  // OR_Gate
  and and_11 (and_11_out, or_5_out, Q[2], u_d, npe);
  and and_12 (and_12_out, ~npe, P[2]);  // AND_Gate
  and and_13 (and_13_out, ~Q[0], ~Q[1], ~Q[2], and_1_out, ~u_d, npe);  // AND_Gate
  or or_6 (or_6_out, and_10_out, and_11_out, and_12_out, and_13_out, and_14_out);
  D_Flip_Flop d_ff_3 (.clk(clk), .D(or_6_out), .Q(Q[2]));  // open: Qn, preset, en, reset
  or or_7 (or_7_out, ~and_1_out, Q[0], Q[1]);  // OR_Gate
  and and_14 (and_14_out, or_7_out, Q[2], ~u_d, npe);  // AND_Gate
  or or_8 (or_8_out, ~and_1_out, ~Q[0], ~Q[1], ~Q[2]);  // OR_Gate
  and and_15 (and_15_out, Q[0], Q[1], Q[2], ~Q[3], and_1_out, u_d, npe);  // AND_Gate
  and and_16 (and_16_out, ~npe, P[3]);  // AND_Gate
  and and_17 (and_17_out, or_8_out, Q[3], u_d, npe);
  or or_9 (or_9_out, and_15_out, and_17_out, and_16_out, and_18_out, and_19_out);
  or or_10 (or_10_out, ~and_1_out, Q[0], Q[1], Q[2]);  // OR_Gate
  and and_18 (and_18_out, ~Q[0], ~Q[1], ~Q[2], ~Q[3], and_1_out, ~u_d, npe);  // AND_Gate
  D_Flip_Flop d_ff_4 (.clk(clk), .D(or_9_out), .Q(Q[3]));  // open: Qn, preset, en, reset
  and and_19 (and_19_out, or_10_out, Q[3], ~u_d, npe);  // AND_Gate
  and and_20 (and_20_out, u_d, ~ncet, Q[0], Q[1], Q[2], Q[3]);  // AND_Gate
  and and_21 (and_21_out, ~u_d, ~ncet, ~Q[0], ~Q[1], ~Q[2], ~Q[3]);  // AND_Gate
  nor nor_1 (ntc, and_20_out, and_21_out);
endmodule

module _181 (
  input  [3:0] nA,
  input  [3:0] nB,
  input  [3:0] S,
  input  m,
  input  cn,
  output cn_4,
  output zero,
  output ng,
  output np,
  output [3:0] nF
);

  wire and_1_out, and_2_out, and_3_out, and_4_out, and_5_out, and_6_out, and_7_out, and_8_out, and_9_out,
       and_10_out, and_11_out, and_12_out, and_13_out, and_14_out, and_15_out, and_16_out, and_17_out,
       and_18_out, and_19_out, and_20_out, and_21_out, and_22_out, and_23_out, and_24_out, and_26_out,
       and_27_out, and_28_out, and_29_out, nand_1_out, nand_3_out, nor_1_out, nor_2_out, nor_3_out,
       nor_4_out, nor_5_out, nor_6_out, nor_7_out, nor_8_out, nor_9_out, nor_10_out, nor_11_out, not_1_out,
       xor_2_out, xor_3_out, xor_5_out, xor_8_out;

  and and_1 (and_1_out, nB[0], S[0]);
  nor nor_1 (nor_1_out, nA[0], and_1_out, and_2_out);
  not not_1 (not_1_out, m);
  nand nand_1 (nand_1_out, cn, not_1_out);
  xor xor_1 (nF[0], nand_1_out, xor_2_out);
  and and_2 (and_2_out, ~nB[0], S[1]);  // AND_Gate
  and and_3 (and_3_out, nA[0], ~nB[0], S[2]);  // AND_Gate
  and and_4 (and_4_out, nor_1_out, not_1_out);
  and and_5 (and_5_out, cn, nor_4_out, not_1_out);
  nor nor_2 (nor_2_out, and_4_out, and_5_out);
  xor xor_2 (xor_2_out, nor_1_out, nor_4_out);
  and and_6 (and_6_out, nB[1], S[0]);
  and and_7 (and_7_out, nA[0], nB[0], S[3]);
  nor nor_3 (nor_3_out, nA[1], and_6_out, and_10_out);
  nor nor_4 (nor_4_out, and_3_out, and_7_out);
  and and_8 (and_8_out, nor_3_out, not_1_out);
  xor xor_3 (xor_3_out, nor_3_out, nor_7_out);
  xor xor_4 (nF[1], nor_2_out, xor_3_out);
  and and_9 (and_9_out, nA[1], ~nB[1], S[2]);  // AND_Gate
  and and_10 (and_10_out, ~nB[1], S[1]);  // AND_Gate
  and and_11 (and_11_out, cn, nor_4_out, nor_7_out, not_1_out);
  and and_12 (and_12_out, nor_1_out, nor_7_out, not_1_out);
  nor nor_5 (nor_5_out, and_8_out, and_12_out, and_11_out);
  and and_13 (and_13_out, nB[2], S[0]);
  and and_14 (and_14_out, nA[1], nB[1], S[3]);
  nor nor_6 (nor_6_out, nA[2], and_13_out, and_17_out);
  nor nor_7 (nor_7_out, and_9_out, and_14_out);
  and and_15 (and_15_out, nor_6_out, not_1_out);
  xor xor_5 (xor_5_out, nor_6_out, nor_10_out);
  xor xor_6 (nF[2], nor_5_out, xor_5_out);
  and and_16 (and_16_out, nA[2], ~nB[2], S[2]);  // AND_Gate
  and and_17 (and_17_out, ~nB[2], S[1]);  // AND_Gate
  and and_18 (and_18_out, nor_3_out, nor_10_out, not_1_out);
  and and_19 (and_19_out, nor_1_out, nor_7_out, nor_10_out, not_1_out);
  nor nor_8 (nor_8_out, and_15_out, and_18_out, and_19_out, and_22_out);
  and and_20 (and_20_out, nB[3], S[0]);
  and and_21 (and_21_out, nA[2], nB[2], S[3]);
  nor nor_9 (nor_9_out, nA[3], and_20_out, and_24_out);
  nor nor_10 (nor_10_out, and_16_out, and_21_out);
  and and_22 (and_22_out, cn, nor_4_out, nor_7_out, nor_10_out, not_1_out);
  xor xor_7 (nF[3], nor_8_out, xor_8_out);
  and and_23 (and_23_out, nA[3], ~nB[3], S[2]);  // AND_Gate
  and and_24 (and_24_out, ~nB[3], S[1]);  // AND_Gate
  nand nand_2 (np, nor_4_out, nor_7_out, nor_10_out, nor_11_out);
  xor xor_8 (xor_8_out, nor_9_out, nor_11_out);
  and and_25 (zero, nF[0], nF[1], nF[2], nF[3]);
  and and_26 (and_26_out, nA[3], nB[3], S[3]);
  nor nor_11 (nor_11_out, and_23_out, and_26_out);
  nand nand_3 (nand_3_out, cn, nor_4_out, nor_7_out, nor_10_out, nor_11_out);
  and and_27 (and_27_out, nor_3_out, nor_10_out, nor_11_out);
  and and_28 (and_28_out, nor_1_out, nor_7_out, nor_10_out, nor_11_out);
  nor nor_12 (ng, and_28_out, and_27_out, and_29_out, nor_9_out);
  and and_29 (and_29_out, nor_6_out, nor_11_out);
  or or_1 (cn_4, ~nand_3_out, ~ng);  // OR_Gate

  // Notes on the sheet:
  //   and_25 drives only 0 and floats otherwise
endmodule

module _182 (
  input  ng0,
  input  np0,
  input  ng1,
  input  np1,
  input  ng2,
  input  np2,
  input  ng3,
  input  np3,
  input  cn,
  output cn_x,
  output cn_y,
  output cn_z,
  output ng,
  output np
);

  wire and_1_out, and_2_out, and_3_out, and_4_out, and_5_out, and_6_out, and_7_out, and_8_out, and_9_out,
       and_10_out, and_11_out, and_12_out, and_13_out, not_1_out;

  not not_1 (not_1_out, cn);
  and and_1 (and_1_out, ng0, not_1_out);
  and and_2 (and_2_out, ng0, np0);
  nor nor_1 (cn_x, and_2_out, and_1_out);
  and and_3 (and_3_out, ng0, np0, ng1);
  and and_4 (and_4_out, ng1, np1);
  nor nor_2 (cn_y, and_4_out, and_3_out, and_5_out);
  and and_5 (and_5_out, ng0, ng1, not_1_out);
  and and_6 (and_6_out, ng2, np2);
  and and_7 (and_7_out, ng1, np1, ng2);
  nor nor_3 (cn_z, and_6_out, and_7_out, and_8_out, and_9_out);
  and and_8 (and_8_out, ng0, np0, ng1, ng2);
  and and_9 (and_9_out, ng0, ng1, ng2, not_1_out);
  and and_10 (and_10_out, ng3, np3);
  and and_11 (and_11_out, ng2, np2, ng3);
  or or_1 (ng, and_10_out, and_11_out, and_13_out, and_12_out);
  and and_12 (and_12_out, ng0, ng1, ng2, ng3);
  and and_13 (and_13_out, ng1, np1, ng2, ng3);
  or or_2 (np, np0, np1, np2, np3);
endmodule

// 279
module _279_1 (
  input  nr,
  input  ns1,
  input  ns2,
  output q
);

  wire nand_1_out;

  nand nand_1 (nand_1_out, nr, q);
  nand nand_2 (q, nand_1_out, ns1, ns2);
endmodule

// 279
module _279_2 (
  input  nr,
  input  ns,
  output q
);

  wire nand_1_out;

  nand nand_1 (nand_1_out, nr, q);
  nand nand_2 (q, nand_1_out, ns);
endmodule

module _377 (
  input  [7:0] D,
  input  clk,
  input  ng,
  output [7:0] Q
);

  wire and_1_out, and_2_out;

  and and_1 (and_1_out, clk, ~and_2_out);  // AND_Gate
  and and_2 (and_2_out, ~and_1_out, ~ng);  // AND_Gate
  D_Flip_Flop d_ff_1 (.clk(clk), .D(D[0]), .Q(Q[0]), .en(and_2_out));  // open: Qn, preset, reset
  D_Flip_Flop d_ff_2 (.clk(clk), .D(D[1]), .Q(Q[1]), .en(and_2_out));  // open: Qn, preset, reset
  D_Flip_Flop d_ff_3 (.clk(clk), .D(D[2]), .Q(Q[2]), .en(and_2_out));  // open: Qn, preset, reset
  D_Flip_Flop d_ff_4 (.clk(clk), .D(D[3]), .Q(Q[3]), .en(and_2_out));  // open: Qn, preset, reset
  D_Flip_Flop d_ff_5 (.clk(clk), .D(D[4]), .Q(Q[4]), .en(and_2_out));  // open: Qn, preset, reset
  D_Flip_Flop d_ff_6 (.clk(clk), .D(D[5]), .Q(Q[5]), .en(and_2_out));  // open: Qn, preset, reset
  D_Flip_Flop d_ff_7 (.clk(clk), .D(D[6]), .Q(Q[6]), .en(and_2_out));  // open: Qn, preset, reset
  D_Flip_Flop d_ff_8 (.clk(clk), .D(D[7]), .Q(Q[7]), .en(and_2_out));  // open: Qn, preset, reset
endmodule

module _641 (
  input  [7:0] A,
  input  a_b,
  input  ng,
  input  [7:0] B,
  output [7:0] A_2,
  output [7:0] B_2
);

  wire and_1_out, and_2_out;

  and and_1 (and_1_out, a_b, ~ng);  // AND_Gate
  nand nand_1 (B_2[0], and_1_out, ~A[0]);  // NAND_Gate
  and and_2 (and_2_out, ~a_b, ~ng);  // AND_Gate
  nand nand_2 (A_2[0], and_2_out, ~B[0]);  // NAND_Gate
  nand nand_3 (B_2[1], and_1_out, ~A[1]);  // NAND_Gate
  nand nand_4 (A_2[1], and_2_out, ~B[1]);  // NAND_Gate
  nand nand_5 (B_2[2], and_1_out, ~A[2]);  // NAND_Gate
  nand nand_6 (A_2[2], and_2_out, ~B[2]);  // NAND_Gate
  nand nand_7 (B_2[3], and_1_out, ~A[3]);  // NAND_Gate
  nand nand_8 (A_2[3], and_2_out, ~B[3]);  // NAND_Gate
  nand nand_9 (B_2[4], and_1_out, ~A[4]);  // NAND_Gate
  nand nand_10 (A_2[4], and_2_out, ~B[4]);  // NAND_Gate
  nand nand_11 (B_2[5], and_1_out, ~A[5]);  // NAND_Gate
  nand nand_12 (A_2[5], and_2_out, ~B[5]);  // NAND_Gate
  nand nand_13 (B_2[6], and_1_out, ~A[6]);  // NAND_Gate
  nand nand_14 (A_2[6], and_2_out, ~B[6]);  // NAND_Gate
  nand nand_15 (B_2[7], and_1_out, ~A[7]);  // NAND_Gate
  nand nand_16 (A_2[7], and_2_out, ~B[7]);  // NAND_Gate

  // Notes on the sheet:
  //   nand_1 drives only 0 and floats otherwise
  //   nand_2 drives only 0 and floats otherwise
  //   nand_3 drives only 0 and floats otherwise
  //   nand_4 drives only 0 and floats otherwise
  //   nand_5 drives only 0 and floats otherwise
  //   nand_6 drives only 0 and floats otherwise
  //   nand_7 drives only 0 and floats otherwise
  //   nand_8 drives only 0 and floats otherwise
  //   nand_9 drives only 0 and floats otherwise
  //   nand_10 drives only 0 and floats otherwise
  //   nand_11 drives only 0 and floats otherwise
  //   nand_12 drives only 0 and floats otherwise
  //   nand_13 drives only 0 and floats otherwise
  //   nand_14 drives only 0 and floats otherwise
  //   nand_15 drives only 0 and floats otherwise
  //   nand_16 drives only 0 and floats otherwise
endmodule

module _62256 (
  input  [7:0] D,
  input  clk,
  input  ncs,
  input  noe,
  input  nwe,
  input  [14:0] A,
  output [7:0] D_2
);

  wire and_1_out, and_2_out, not_1_out;
  wire [7:0] controlled_buffer_1_out;

  and and_1 (and_1_out, ~ncs, ~noe, nwe);  // AND_Gate
  and and_2 (and_2_out, ~ncs, ~nwe);  // AND_Gate
  not not_1 (not_1_out, and_2_out);
  assign controlled_buffer_1_out = and_2_out ? D : 8'bz;  // Controlled_Buffer controlled_buffer_1
  RAM #(.addrWidth(15)) ram_1 (
    .addr(A), .data(controlled_buffer_1_out), .clk(clk), .ld(not_1_out), .clr(1'b0));  // open: sel
  assign D_2 = and_1_out ? controlled_buffer_1_out : 8'bz;  // Controlled_Buffer controlled_buffer_2
endmodule

module Toggle_Switch (
  input  in_1
);
endmodule
