// Logisim project CPU.circ as structural Verilog: 19 circuits, main circuit CPU
module CPU (
  input  run,
  input  step,
  input  al,
  input  exam,
  input  dep,
  input  [15:0] S
);

  wire alu_board_1_p10, clock_1_out, control_board_1_p13, control_board_1_p14, control_board_1_p15,
       control_board_1_p16, not_3_out, not_5_out, not_6_out, not_7_out, not_10_out, not_12_out, not_13_out,
       not_16_out, ram_decoder_board_1__0xxx, ram_decoder_board_1__1xxx;
  wire [1:0] alu_board_1_p3;
  wire [6:0] control_board_1_p12, not_11_out;
  wire [15:0] alu_board_1_p7, alu_board_1_p8, alu_board_1_p9, not_1_out, not_2_out, not_4_out, not_8_out,
       not_9_out, not_14_out, not_15_out, not_17_out, not_18_out, pull_resistor_1_node, pull_resistor_2_node,
       register_board_1_p5, register_board_1_p7;

  Pull_Resistor #(.pull(1)) pull_resistor_1 (.node(pull_resistor_1_node));
  Clock clock_1 (.out(clock_1_out));
  assign not_1_out = ~pull_resistor_1_node;  // NOT_Gate not_1, 16 bits wide
  // Probe on not_1_out
  Pull_Resistor #(.pull(1)) pull_resistor_2 (.node(pull_resistor_2_node));
  assign not_2_out = ~pull_resistor_2_node;  // NOT_Gate not_2, 16 bits wide
  // Probe on not_2_out
  RAM_Decoder_Board ram_decoder_board_1 (
    ._0xxx(ram_decoder_board_1__0xxx), ._1xxx(ram_decoder_board_1__1xxx), .nData(pull_resistor_1_node),
    .nData_2(pull_resistor_1_node), .clk(clock_1_out), .nAddress(pull_resistor_2_node), .nr_w(alu_board_1_p3));  // open: _2xxx, _3xxx, _4xxx, _5xxx, _6xxx, _7xxx
  not not_3 (not_3_out, run);
  // ALU_Board alu_board_1: pin names not known; wires that end beside it: clock_1_out, ram_decoder_board_1__1xxx, alu_board_1_p3, pull_resistor_1_node, pull_resistor_2_node, pull_resistor_1_node, alu_board_1_p7, alu_board_1_p8, alu_board_1_p9, alu_board_1_p10
  assign not_4_out = ~alu_board_1_p7;  // NOT_Gate not_4, 16 bits wide
  // Probe on not_4_out
  not not_5 (not_5_out, al);
  not not_6 (not_6_out, exam);
  not not_7 (not_7_out, step);
  assign not_8_out = ~alu_board_1_p9;  // NOT_Gate not_8, 16 bits wide
  assign not_9_out = ~alu_board_1_p8;  // NOT_Gate not_9, 16 bits wide
  // Probe on not_9_out
  // Probe on not_8_out
  not not_10 (not_10_out, dep);
  // Control_Board control_board_1: pin names not known; wires that end beside it: clock_1_out, ram_decoder_board_1__0xxx, not_3_out, not_7_out, not_5_out, not_6_out, not_10_out, alu_board_1_p10, alu_board_1_p3, pull_resistor_2_node, pull_resistor_2_node, control_board_1_p12, control_board_1_p13, control_board_1_p14, control_board_1_p15, control_board_1_p16, alu_board_1_p3, alu_board_1_p3, alu_board_1_p3
  assign not_11_out = ~control_board_1_p12;  // NOT_Gate not_11, 7 bits wide
  // Probe on not_11_out
  not not_12 (not_12_out, control_board_1_p15);
  not not_13 (not_13_out, control_board_1_p14);
  // Probe on not_13_out
  // Probe on not_12_out
  assign not_14_out = ~S;  // NOT_Gate not_14, 16 bits wide
  // Register_Board register_board_1: pin names not known; wires that end beside it: control_board_1_p14, control_board_1_p16, control_board_1_p13, pull_resistor_2_node, register_board_1_p5, register_board_1_p5, register_board_1_p7
  assign not_15_out = ~register_board_1_p5;  // NOT_Gate not_15, 16 bits wide
  not not_16 (not_16_out, control_board_1_p16);
  // Probe on not_16_out
  // Probe on not_15_out
  assign not_17_out = ~register_board_1_p5;  // NOT_Gate not_17, 16 bits wide
  assign not_18_out = ~register_board_1_p7;  // NOT_Gate not_18, 16 bits wide
  // Probe on not_18_out
  // Probe on not_17_out
endmodule

module Control_Board (
  input  clk,
  input  clk_2,
  input  ng,
  input  [1:0] nr_w,
  input  nrun,
  input  nstep,
  input  nal,
  input  nexam,
  input  c,
  input  ndep,
  input  [15:0] nAddress,
  input  ng_2,
  input  [2:0] flags,
  input  [15:0] nAddress_2,
  output neF,
  output nwA,
  output nwB,
  output [3:0] S,
  output m,
  output cin,
  output [1:0] nr_w_2,
  output nc,
  output nz,
  output nn,
  output ns_d,
  output nd_t,
  output nt_d,
  output nd_x,
  output nx_plus,
  output nx_a,
  output nd_p,
  output np_d,
  output np_a,
  output [6:0] nState
);

  wire _04_3_out, _11_3_out, _21_2_out, _21_out, _32_11_out, _32_out, _40_2_out, n151_1_ny, undriven,
       undriven_2, undriven_3, undriven_4, undriven_5;
  wire [7:0] n377_1_p3, n377_3_p4;
  wire [7:4] n377_2_p6;
  wire [7:7] n377_1_p4;

  not _04 (nc, flags[0]);
  not _04_2 (nz, flags[1]);
  not _04_3 (_04_3_out, flags[2]);
  // _377 377_1: pin names not known; wires that end beside it: 1'b0, clk, {n377_1_p3[7:4], nState[4], nState[5], nState[6], n377_1_p3[0]}, {n377_1_p4[7], nState[0], nState[1], nState[2], nState[3], nState[4], nState[5], nState[6]}, nState[6], nState[6]
  nand _40 (n377_1_p3[7], nstep, nal, nexam, ndep);
  _151 u_151_1 (
    .a(nAddress_2[0]), .b(nAddress_2[1]), .c(nAddress_2[2]), .ng(ng_2), .d0(flags[2]), .d1(_04_3_out),
    .d2(nz), .d3(flags[1]), .d4(nc), .d5(flags[0]), .d6(1'b0), .d7(1'b1), .ny(n151_1_ny));  // open: y
  nand _40_2 (_40_2_out, 1'b1, nState[6], nState[5], nState[4]);
  or _32 (_32_out, n377_1_p4[7], nstep);
  or _32_2 (n377_1_p3[4], n377_1_p4[7], nal);
  or _32_3 (n377_1_p3[5], n377_1_p4[7], nexam);
  or _32_4 (n377_1_p3[6], n377_1_p4[7], ndep);
  and _21 (_21_out, nState[6], nState[5], nState[4], nState[1]);
  and _21_2 (_21_2_out, nState[3], nState[0], 1'b1, 1'b1);
  and _08 (ns_d, nState[2], nState[0]);
  and _08_2 (nd_t, nState[5], nState[1]);
  and _11 (nd_x, nState[6], nState[4], nState[2]);
  and _08_3 (nx_plus, nState[1], nState[0]);
  and _11_2 (nx_a, undriven_3, nState[5], nState[1]);
  or _32_5 (nd_p, undriven_4, undriven_5);
  or _32_6 (np_d, undriven, undriven_2);
  and _08_4 (np_a, nState[4], nState[6]);
  or _32_7 (n377_1_p3[0], _40_2_out, _11_3_out);
  and _11_3 (_11_3_out, nrun, 1'b1, _32_out);
  or _32_8 (neF, ng, nr_w[0]);
  or _32_9 (clk_2, ng, nr_w[1]);
  or _32_10 (nwB, clk_2, nAddress[6]);
  or _32_11 (_32_11_out, clk_2, nAddress[7]);
  // _377 377_2: pin names not known; wires that end beside it: clk_2, clk_2, nwB, neF, {2'b00, nAddress[5:0]}, {n377_2_p6, S}, clk_2, nwB
  // _377 377_3: pin names not known; wires that end beside it: _32_11_out, clk_2, {{7{1'b0}}, c}, n377_3_p4, n377_3_p4[0], n377_3_p4[0]
  _153 u_153_1 (
    .a(n377_2_p6[4]), .b(n377_2_p6[5]), ._1g(1'b1), ._1c0(1'b1), ._1c1(1'b1), ._1c2(1'b1), ._1c3(1'b1),
    ._2g(1'b1), ._2c0(1'b1), ._2c1(1'b1), ._2c2(n377_3_p4[0]), ._2c3(1'b1), ._1y(m), ._2y(cin));

  assign nn = flags[2];
  assign nt_d = nState[3];
  assign nwA = clk_2;
endmodule

// Reg Board
module Register_Board (
  input  [15:0] nData,
  input  clk,
  input  [15:0] nS,
  input  ns_d,
  input  nd_t,
  input  nt_d,
  input  nd_x,
  input  nx_plus,
  input  nx_a,
  input  nd_p,
  input  np_d,
  input  np_a,
  output [15:0] nData_2,
  output [15:0] nT,
  output [15:0] nX,
  output [15:0] nP,
  output [15:0] nAddress
);

  OC_Buffer oc_buffer_1 (.ng(ns_d), .A(nS), .B(nData_2));
  Register register_1 (.clk(clk), .Q(nT), .nwe(nd_t), .D(nData));
  OC_Buffer oc_buffer_2 (.ng(nt_d), .A(nT), .B(nData_2));
  Counter counter_1 (.nwe(nd_x), .nce(nx_plus), .u_d(1'b0), .clk(clk), .Q(nX), .P(nData));  // open: ntc
  OC_Buffer oc_buffer_3 (.ng(nx_a), .A(nX), .B(nAddress));
  Counter counter_2 (.nwe(nd_p), .nce(np_a), .u_d(1'b0), .clk(clk), .Q(nP), .P(nData));  // open: ntc
  OC_Buffer oc_buffer_4 (.ng(np_d), .A(nP), .B(nData_2));
  OC_Buffer oc_buffer_5 (.ng(np_a), .A(nP), .B(nAddress));
endmodule

// RAM&Decoder
module RAM_Decoder_Board (
  input  [15:0] nData,
  input  clk,
  input  [1:0] nr_w,
  input  [15:0] nAddress,
  output [15:0] nData_2,
  output _0xxx,
  output _1xxx,
  output _2xxx,
  output _3xxx,
  output _4xxx,
  output _5xxx,
  output _6xxx,
  output _7xxx
);

  wire n153_1__1y, n153_1__2y, n62256_1_p11, n62256_1_p14, n62256_1_p16, n62256_1_p19, n62256_1_p21,
       n62256_1_p27, n62256_2_p13, n62256_2_p14, n62256_2_p15, n62256_2_p16, n62256_2_p17, n62256_2_p18,
       n62256_2_p19, n62256_2_p20;
  wire [7:0] n62256_1_p13, n62256_1_p29;

  _153 u_153_1 (
    .a(nAddress[15]), .b(nAddress[15]), ._1g(1'b0), ._1c0(1'b1), ._1c1(1'b1), ._1c2(nAddress[15]),
    ._1c3(1'b1), ._2g(1'b0), ._2c0(nAddress[15]), ._2c1(nAddress[15]), ._2c2(nAddress[15]), ._2c3(1'b1),
    ._1y(n153_1__1y), ._2y(n153_1__2y));
  // _62256 62256_1: pin names not known; wires that end beside it: {nAddress[14:1], nAddress[15]}, {nAddress[14:1], nAddress[15]}, {nAddress[14:1], nAddress[15]}, {nAddress[14:1], nAddress[15]}, {nAddress[14:1], nAddress[15]}, {nAddress[14:1], nAddress[15]}, {nAddress[14:1], nAddress[15]}, {nAddress[14:1], nAddress[15]}, {nAddress[14:1], nAddress[15]}, clk, n62256_1_p11, {nAddress[14:1], nAddress[15]}, n62256_1_p13, n62256_1_p14, {nAddress[14:1], nAddress[15]}, n62256_1_p16, {nAddress[14:1], nAddress[15]}, n62256_1_p13, n62256_1_p19, {nAddress[14:1], nAddress[15]}, n62256_1_p21, {nAddress[14:1], nAddress[15]}, {nAddress[14:1], nAddress[15]}, {nAddress[14:1], nAddress[15]}, {nAddress[14:1], nAddress[15]}, {nAddress[14:1], nAddress[15]}, n62256_1_p27, clk, n62256_1_p29, n62256_1_p29
  OC_Transceiver oc_transceiver_1 (
    .ng(n153_1__2y), .A(nData), .A_2(nData_2), .B_2({n62256_1_p29, n62256_1_p13}),
    .B({n62256_1_p29, n62256_1_p13}), .a_b(n153_1__1y));
  // _62256 62256_2: pin names not known; wires that end beside it: n62256_1_p13, clk, clk, clk, {nAddress[14:1], nAddress[15]}, {nAddress[14:1], nAddress[15]}, {nAddress[14:1], nAddress[15]}, n62256_1_p27, {nAddress[14:1], nAddress[15]}, n62256_1_p29, n62256_1_p13, n62256_1_p29, n62256_2_p13, n62256_2_p14, n62256_2_p15, n62256_2_p16, n62256_2_p17, n62256_2_p18, n62256_2_p19, n62256_2_p20
  Pull_Resistor #(.pull(1)) pull_resistor_1 (.node({n62256_1_p29, n62256_1_p13}));
  _138 u_138_1 (
    .a(nAddress[12]), .b(nAddress[13]), .c(nAddress[14]), .g1(nAddress[15]), .ng2a(1'b0), .ng2b(1'b0),
    .ny0(_7xxx), .ny1(_3xxx), .ny2(_3xxx), .ny3(_3xxx), .ny4(_3xxx), .ny5(_2xxx), .ny6(_1xxx), .ny7(_0xxx));
  // Pins of 1 and 15 bits meet at {nAddress[14:1], nAddress[15]}

  assign _4xxx = _3xxx;
  assign _5xxx = _3xxx;
  assign _6xxx = _3xxx;
  assign nAddress[0] = nAddress[15];
  assign nr_w = {2{nAddress[15]}};
endmodule

module ALU_Board (
  input  clk,
  input  [15:0] nData,
  input  neF,
  input  nwA,
  input  nwB,
  input  [3:0] S,
  input  m,
  input  cin,
  output [15:0] nData_2,
  output [15:0] nA,
  output [15:0] nB,
  output [15:0] nF,
  output [2:0] flags
);

  Register register_1 (.clk(clk), .Q(nA), .nwe(nwA), .D(nData));
  ALU alu_1 ();
  OC_Buffer oc_buffer_1 (.ng(neF), .A({flags[2], nF[14:0]}), .B(nData_2));
  Register register_2 (.clk(clk), .Q(nB), .nwe(nwB), .D({flags[2], nF[14:0]}));

  assign nF[15] = flags[2];
endmodule

// OCB
module OC_Buffer (
  input  [15:0] A,
  input  ng,
  output [15:0] B
);

  wire n641_1_p1, n641_1_p2, n641_1_p4, n641_1_p5, n641_1_p6, n641_1_p7, n641_1_p8, n641_1_p12, n641_1_p13,
       n641_1_p17, n641_1_p18, n641_2_p1, n641_2_p2, n641_2_p4, n641_2_p5, n641_2_p7, n641_2_p8, n641_2_p12,
       n641_2_p13, n641_2_p18;

  // _641 641_1: pin names not known; wires that end beside it: n641_1_p1, n641_1_p2, 1'b1, n641_1_p4, n641_1_p5, n641_1_p6, n641_1_p7, n641_1_p8, A[15:8], A[15:8], A[15:8], n641_1_p12, n641_1_p13, B[15:8], B[15:8], B[15:8], n641_1_p17, n641_1_p18
  // _641 641_2: pin names not known; wires that end beside it: n641_2_p1, n641_2_p2, 1'b1, n641_2_p4, n641_2_p5, B[15:8], n641_2_p7, n641_2_p8, A[15:8], A[15:8], A[15:8], n641_2_p12, n641_2_p13, B[15:8], B[15:8], B[15:8], B[15:8], n641_2_p18
  // Pins of 1 and 8 bits meet at A[15:8]

  assign A[7:0] = A[15:8];
  assign B[7:0] = B[15:8];
  assign ng = A[8];
endmodule

// OCT
module OC_Transceiver (
  input  [15:0] A,
  input  ng,
  input  a_b,
  input  [15:0] B,
  output [15:0] A_2,
  output [15:0] B_2
);

  wire n641_1_p1, n641_1_p2, n641_1_p4, n641_1_p8, n641_1_p12, n641_1_p13, n641_1_p18, n641_2_p1, n641_2_p2,
       n641_2_p4, n641_2_p5, n641_2_p8, n641_2_p11, n641_2_p12, n641_2_p17;

  // _641 641_1: pin names not known; wires that end beside it: n641_1_p1, n641_1_p2, {B[15:9], a_b}, n641_1_p4, {B[15:9], a_b}, B_2[7:0], {B[15:9], a_b}, n641_1_p8, A[15:8], A[15:8], A[15:8], n641_1_p12, n641_1_p13, {B[15:9], a_b}, {B[15:9], a_b}, {B[15:9], a_b}, {B[15:9], a_b}, n641_1_p18
  // _641 641_2: pin names not known; wires that end beside it: n641_2_p1, n641_2_p2, {B[15:9], a_b}, n641_2_p4, n641_2_p5, {B[15:9], a_b}, {B[15:9], a_b}, n641_2_p8, A[15:8], A_2[15:8], n641_2_p11, n641_2_p12, {B[15:9], a_b}, {B[15:9], a_b}, {B[15:9], a_b}, {B[15:9], a_b}, n641_2_p17
  // Pins of 1 and 8 bits meet at {B[15:9], a_b}
  // Pins of 1 and 8 bits meet at A[15:8]

  assign A[7:0] = A[15:8];
  assign A_2[7:0] = A[15:8];
  assign B[8:0] = {a_b, B[15:9], a_b};
  assign B_2[15:8] = {B[15:9], a_b};
  assign ng = A[8];
endmodule

// Reg
module Register (
  input  [15:0] D,
  input  clk,
  input  nwe,
  output [15:0] Q
);

  // _377 377_1: pin names not known; wires that end beside it: {D[7:1], clk}, nwe, D[15:8], {D[7:1], clk}, nwe, Q[15:8]
  // _377 377_2: pin names not known; wires that end beside it: nwe, {D[7:1], clk}, Q[15:8], D[15:8], D[15:8], Q[15:8], Q[15:8]
  // Pins of 1 and 8 bits meet at {D[7:1], clk}

  assign D[0] = clk;
  assign Q[7:0] = Q[15:8];
endmodule

// Ctr
module Counter (
  input  [15:0] P,
  input  clk,
  input  nwe,
  input  u_d,
  input  nce,
  output ntc,
  output [15:0] Q
);

  wire n169_1_ntc, n169_2_ntc, n169_3_ntc;

  _169 u_169_1 (.clk(clk), .npe(nwe), .u_d(u_d), .ncet(nce), .ncep(nce), .ntc(n169_1_ntc), .P(P[3:0]), .Q(Q[3:0]));
  _169 u_169_2 (
    .clk(clk), .npe(nwe), .u_d(u_d), .ncet(nce), .ncep(n169_1_ntc), .ntc(n169_2_ntc), .P(P[7:4]), .Q(Q[7:4]));
  _169 u_169_3 (
    .clk(clk), .npe(nwe), .u_d(u_d), .ncet(n169_2_ntc), .ncep(n169_1_ntc), .ntc(n169_3_ntc), .P(P[11:8]),
    .Q(Q[11:8]));
  _169 u_169_4 (
    .clk(clk), .npe(nwe), .u_d(u_d), .ncet(n169_3_ntc), .ncep(n169_1_ntc), .ntc(ntc), .P(P[15:12]),
    .Q(Q[15:12]));
endmodule

module ALU (
);

  wire n181_1_ng, n181_1_np, n181_1_zero, n181_2_ng, n181_2_np, n181_3_ng, n181_3_np, n181_3_zero, n181_4_ng,
       n181_4_np, n182_1_cn_x, n182_1_cn_y, n182_1_cn_z, undriven, undriven_2, undriven_3, undriven_4,
       undriven_5, undriven_6;

  _181 u_181_1 (
    .Cn(undriven_6), .M(undriven_5), .ng(n181_1_ng), .np(n181_1_np), .zero(n181_1_zero), .S0(undriven),
    .S1(undriven_2), .S2(undriven_3), .S3(undriven_4));  // open: cn_4, nF0, nF1, nF2, nF3, nA0, nA1, nA2, nA3, nB0, nB1, nB2, nB3
  _181 u_181_2 (
    .Cn(n182_1_cn_x), .M(undriven_5), .ng(n181_2_ng), .np(n181_2_np), .zero(n181_1_zero), .S0(undriven),
    .S1(undriven_2), .S2(undriven_3), .S3(undriven_4));  // open: cn_4, nF0, nF1, nF2, nF3, nA0, nA1, nA2, nA3, nB0, nB1, nB2, nB3
  _181 u_181_3 (
    .Cn(n182_1_cn_y), .M(undriven_5), .ng(n181_3_ng), .np(n181_3_np), .zero(n181_3_zero), .S0(undriven),
    .S1(undriven_2), .S2(undriven_3), .S3(undriven_4));  // open: cn_4, nF0, nF1, nF2, nF3, nA0, nA1, nA2, nA3, nB0, nB1, nB2, nB3
  _182 u_182_1 (
    .Cn(undriven_6), .nG0(n181_1_ng), .nP0(n181_1_np), .nG1(n181_2_ng), .nP1(n181_2_np), .nG2(n181_3_ng),
    .nP2(n181_3_np), .nG3(n181_4_ng), .nP3(n181_4_np), .Cn_x(n182_1_cn_x), .Cn_y(n182_1_cn_y),
    .Cn_z(n182_1_cn_z));  // open: nG, nP
  _181 u_181_4 (
    .Cn(n182_1_cn_z), .M(undriven_5), .ng(n181_4_ng), .np(n181_4_np), .zero(n181_3_zero), .S0(undriven),
    .S1(undriven_2), .S2(undriven_3), .S3(undriven_4));  // open: cn_4, nF0, nF1, nF2, nF3, nA0, nA1, nA2, nA3, nB0, nB1, nB2, nB3
endmodule

module _138 (
  input  a,
  input  b,
  input  c,
  input  g1,
  input  ng2a,
  input  ng2b,
  output ny0,
  output ny1,
  output ny2,
  output ny3,
  output ny4,
  output ny5,
  output ny6,
  output ny7
);

  wire and_1_out;

  and and_1 (and_1_out, g1, ~ng2a, ~ng2b);  // AND_Gate
  nand nand_1 (ny0, ~a, ~b, ~c, and_1_out);  // NAND_Gate
  nand nand_2 (ny1, a, ~b, ~c, and_1_out);  // NAND_Gate
  nand nand_3 (ny2, ~a, b, ~c, and_1_out);  // NAND_Gate
  nand nand_4 (ny3, a, b, ~c, and_1_out);  // NAND_Gate
  nand nand_5 (ny4, ~a, ~b, c, and_1_out);  // NAND_Gate
  nand nand_6 (ny5, a, ~b, c, and_1_out);  // NAND_Gate
  nand nand_7 (ny6, ~a, b, c, and_1_out);  // NAND_Gate
  nand nand_8 (ny7, a, b, c, and_1_out);
endmodule

module _151 (
  input  a,
  input  b,
  input  c,
  input  ng,
  input  d0,
  input  d1,
  input  d2,
  input  d3,
  input  d4,
  input  d5,
  input  d6,
  input  d7,
  output y,
  output ny
);

  wire and_1_out, and_2_out, and_3_out, and_4_out, and_5_out, and_6_out, and_7_out, and_8_out;

  and and_1 (and_1_out, d0, ~a, ~b, ~c, ~ng);  // AND_Gate
  and and_2 (and_2_out, d1, a, ~b, ~c, ~ng);  // AND_Gate
  and and_3 (and_3_out, d2, ~a, b, ~c, ~ng);  // AND_Gate
  and and_4 (and_4_out, d3, a, b, ~c, ~ng);  // AND_Gate
  and and_5 (and_5_out, d4, ~a, ~b, c, ~ng);  // AND_Gate
  and and_6 (and_6_out, d5, a, ~b, c, ~ng);  // AND_Gate
  and and_7 (and_7_out, d6, ~a, b, c, ~ng);  // AND_Gate
  and and_8 (and_8_out, d7, a, b, c, ~ng);  // AND_Gate
  or or_1 (y, and_1_out, and_2_out, and_3_out, and_4_out, and_5_out, and_6_out, and_7_out, and_8_out);
  not not_1 (ny, y);
endmodule

module _153 (
  input  a,
  input  b,
  input  _1g,
  input  _1c0,
  input  _1c1,
  input  _1c2,
  input  _1c3,
  input  _2g,
  input  _2c0,
  input  _2c1,
  input  _2c2,
  input  _2c3,
  output _1y,
  output _2y
);

  wire and_1_out, and_2_out, and_3_out, and_4_out, and_5_out, and_6_out, and_7_out, and_8_out;

  and and_1 (and_1_out, ~_1g, ~a, ~b, _1c0);  // AND_Gate
  and and_2 (and_2_out, ~_1g, a, ~b, _1c1);  // AND_Gate
  and and_3 (and_3_out, ~_1g, ~a, b, _1c2);  // AND_Gate
  and and_4 (and_4_out, ~_1g, a, b, _1c3);  // AND_Gate
  and and_5 (and_5_out, ~_2g, ~a, ~b, _2c0);  // AND_Gate
  and and_6 (and_6_out, ~_2g, a, ~b, _2c1);  // AND_Gate
  and and_7 (and_7_out, ~_2g, ~a, b, _2c2);  // AND_Gate
  and and_8 (and_8_out, ~_2g, a, b, _2c3);  // AND_Gate
  or or_1 (_1y, and_1_out, and_2_out, and_3_out, and_4_out);
  or or_2 (_2y, and_5_out, and_6_out, and_7_out, and_8_out);
endmodule

module _169 (
  input  [3:0] P,
  input  clk,
  input  npe,
  input  u_d,
  input  ncet,
  input  ncep,
  output ntc,
  output [3:0] Q
);

  wire and_1_out, and_2_out, and_3_out, and_4_out, and_5_out, and_6_out, and_7_out, and_8_out, and_9_out,
       and_10_out, and_11_out, and_12_out, and_13_out, and_14_out, and_15_out, and_16_out, and_17_out,
       and_18_out, and_19_out, and_20_out, and_21_out, or_1_out, or_2_out, or_3_out, or_4_out, or_5_out,
       or_6_out, or_7_out, or_8_out, or_9_out, or_10_out;

  and and_1 (and_1_out, ~ncet, ~ncep);  // AND_Gate
  and and_2 (and_2_out, ~npe, P[0]);  // AND_Gate
  and and_3 (and_3_out, ~Q[0], and_1_out, npe);  // AND_Gate
  or or_1 (or_1_out, and_3_out, and_2_out, and_5_out);
  and and_4 (and_4_out, Q[0], ~Q[1], and_1_out, u_d, npe);  // AND_Gate
  and and_5 (and_5_out, Q[0], ~and_1_out, npe);  // AND_Gate
  D_Flip_Flop d_ff_1 (.clk(clk), .D(or_1_out), .Q(Q[0]));  // open: Qn, preset, en, reset
  and and_6 (and_6_out, ~npe, P[1]);  // AND_Gate
  or or_2 (or_2_out, ~and_1_out, ~Q[0]);  // OR_Gate
  and and_7 (and_7_out, or_2_out, Q[1], u_d, npe);
  or or_3 (or_3_out, and_4_out, and_7_out, and_6_out, and_8_out, and_10_out);
  or or_4 (or_4_out, ~and_1_out, Q[0]);  // OR_Gate
  and and_8 (and_8_out, ~Q[0], ~Q[1], and_1_out, ~u_d, npe);  // AND_Gate
  D_Flip_Flop d_ff_2 (.clk(clk), .D(or_3_out), .Q(Q[1]));  // open: Qn, preset, en, reset
  and and_9 (and_9_out, Q[0], Q[1], ~Q[2], and_1_out, u_d, npe);  // AND_Gate
  and and_10 (and_10_out, or_4_out, Q[1], ~u_d, npe);  // AND_Gate
  or or_5 (or_5_out, ~and_1_out, ~Q[0], ~Q[1]);  // OR_Gate
  and and_11 (and_11_out, or_5_out, Q[2], u_d, npe);
  and and_12 (and_12_out, ~npe, P[2]);  // AND_Gate
  and and_13 (and_13_out, ~Q[0], ~Q[1], ~Q[2], and_1_out, ~u_d, npe);  // AND_Gate
  or or_6 (or_6_out, and_9_out, and_11_out, and_12_out, and_13_out, and_14_out);
  D_Flip_Flop d_ff_3 (.clk(clk), .D(or_6_out), .Q(Q[2]));  // open: Qn, preset, en, reset
  or or_7 (or_7_out, ~and_1_out, Q[0], Q[1]);  // OR_Gate
  and and_14 (and_14_out, or_7_out, Q[2], ~u_d, npe);  // AND_Gate
  or or_8 (or_8_out, ~and_1_out, ~Q[0], ~Q[1], ~Q[2]);  // OR_Gate
  and and_15 (and_15_out, Q[0], Q[1], Q[2], ~Q[3], and_1_out, u_d, npe);  // AND_Gate
  and and_16 (and_16_out, ~npe, P[3]);  // AND_Gate
  and and_17 (and_17_out, or_8_out, Q[3], u_d, npe);
  or or_9 (or_9_out, and_15_out, and_17_out, and_16_out, and_18_out, and_19_out);
  or or_10 (or_10_out, ~and_1_out, Q[0], Q[1], Q[2]);  // OR_Gate
  and and_18 (and_18_out, ~Q[0], ~Q[1], ~Q[2], ~Q[3], and_1_out, ~u_d, npe);  // AND_Gate
  D_Flip_Flop d_ff_4 (.clk(clk), .D(or_9_out), .Q(Q[3]));  // open: Qn, preset, en, reset
  and and_19 (and_19_out, or_10_out, Q[3], ~u_d, npe);  // AND_Gate
  and and_20 (and_20_out, u_d, ~ncet, Q[0], Q[1], Q[2], Q[3]);  // AND_Gate
  and and_21 (and_21_out, ~u_d, ~ncet, ~Q[0], ~Q[1], ~Q[2], ~Q[3]);  // AND_Gate
  nor nor_1 (ntc, and_20_out, and_21_out);
endmodule

module _181 (
  input  nA0,
  input  nA1,
  input  nA2,
  input  nA3,
  input  nB0,
  input  nB1,
  input  nB2,
  input  nB3,
  input  S0,
  input  S1,
  input  S2,
  input  S3,
  input  M,
  input  Cn,
  output cn_4,
  output zero,
  output ng,
  output np,
  output nF0,
  output nF1,
  output nF2,
  output nF3
);

  wire and_1_out, and_2_out, and_3_out, and_4_out, and_5_out, and_6_out, and_7_out, and_8_out, and_9_out,
       and_10_out, and_11_out, and_12_out, and_13_out, and_14_out, and_15_out, and_16_out, and_17_out,
       and_18_out, and_19_out, and_20_out, and_21_out, and_22_out, and_23_out, and_24_out, and_25_out,
       and_27_out, and_28_out, and_29_out, nand_1_out, nand_3_out, nor_1_out, nor_2_out, nor_3_out,
       nor_4_out, nor_5_out, nor_6_out, nor_7_out, nor_8_out, nor_9_out, nor_10_out, nor_11_out, not_1_out,
       xor_1_out, xor_3_out, xor_5_out, xor_7_out;

  not not_1 (not_1_out, M);
  and and_1 (and_1_out, ~nB0, S1);  // AND_Gate
  and and_2 (and_2_out, nB0, S0);
  nor nor_1 (nor_1_out, nA0, and_2_out, and_1_out);
  and and_3 (and_3_out, nor_1_out, not_1_out);
  nand nand_1 (nand_1_out, Cn, not_1_out);
  xor xor_1 (xor_1_out, nor_1_out, nor_2_out);
  xor xor_2 (nF0, nand_1_out, xor_1_out);
  and and_4 (and_4_out, nB1, S0);
  and and_5 (and_5_out, nA0, nB0, S3);
  and and_6 (and_6_out, nA0, ~nB0, S2);  // AND_Gate
  nor nor_2 (nor_2_out, and_6_out, and_5_out);
  nor nor_3 (nor_3_out, nA1, and_4_out, and_9_out);
  and and_7 (and_7_out, Cn, nor_2_out, not_1_out);
  and and_8 (and_8_out, nor_3_out, not_1_out);
  nor nor_4 (nor_4_out, and_3_out, and_7_out);
  xor xor_3 (xor_3_out, nor_3_out, nor_5_out);
  xor xor_4 (nF1, nor_4_out, xor_3_out);
  and and_9 (and_9_out, ~nB1, S1);  // AND_Gate
  and and_10 (and_10_out, nA1, ~nB1, S2);  // AND_Gate
  nor nor_5 (nor_5_out, and_10_out, and_13_out);
  and and_11 (and_11_out, Cn, nor_2_out, nor_5_out, not_1_out);
  and and_12 (and_12_out, nor_1_out, nor_5_out, not_1_out);
  nor nor_6 (nor_6_out, and_8_out, and_12_out, and_11_out);
  and and_13 (and_13_out, nA1, nB1, S3);
  and and_14 (and_14_out, ~nB2, S1);  // AND_Gate
  and and_15 (and_15_out, nB2, S0);
  nor nor_7 (nor_7_out, nA2, and_15_out, and_14_out);
  and and_16 (and_16_out, nor_7_out, not_1_out);
  xor xor_5 (xor_5_out, nor_7_out, nor_8_out);
  xor xor_6 (nF2, nor_6_out, xor_5_out);
  and and_17 (and_17_out, nA2, nB2, S3);
  and and_18 (and_18_out, nA2, ~nB2, S2);  // AND_Gate
  nor nor_8 (nor_8_out, and_18_out, and_17_out);
  and and_19 (and_19_out, nor_3_out, nor_8_out, not_1_out);
  and and_20 (and_20_out, nor_1_out, nor_5_out, nor_8_out, not_1_out);
  nor nor_9 (nor_9_out, and_16_out, and_19_out, and_20_out, and_24_out);
  and and_21 (and_21_out, nA3, ~nB3, S2);  // AND_Gate
  and and_22 (and_22_out, nB3, S0);
  and and_23 (and_23_out, ~nB3, S1);  // AND_Gate
  nor nor_10 (nor_10_out, nA3, and_22_out, and_23_out);
  and and_24 (and_24_out, Cn, nor_2_out, nor_5_out, nor_8_out, not_1_out);
  xor xor_7 (xor_7_out, nor_10_out, nor_11_out);
  xor xor_8 (nF3, nor_9_out, xor_7_out);
  and and_25 (and_25_out, nA3, nB3, S3);
  nor nor_11 (nor_11_out, and_21_out, and_25_out);
  nand nand_2 (np, nor_2_out, nor_5_out, nor_8_out, nor_11_out);
  nand nand_3 (nand_3_out, Cn, nor_2_out, nor_5_out, nor_8_out, nor_11_out);
  and and_26 (zero, nF0, nF1, nF2, nF3);
  and and_27 (and_27_out, nor_3_out, nor_8_out, nor_11_out);
  and and_28 (and_28_out, nor_1_out, nor_5_out, nor_8_out, nor_11_out);
  and and_29 (and_29_out, nor_7_out, nor_11_out);
  nor nor_12 (ng, and_28_out, and_27_out, and_29_out, nor_10_out);
  or or_1 (cn_4, ~nand_3_out, ~ng);  // OR_Gate

  // Notes on the sheet:
  //   and_26 drives only 0 and floats otherwise
endmodule

module _182 (
  input  nG0,
  input  nP0,
  input  nG1,
  input  nP1,
  input  nG2,
  input  nP2,
  input  nG3,
  input  nP3,
  input  Cn,
  output Cn_x,
  output Cn_y,
  output Cn_z,
  output nG,
  output nP
);

  wire and_1_out, and_2_out, and_3_out, and_4_out, and_5_out, and_6_out, and_7_out, and_8_out, and_9_out,
       and_10_out, and_11_out, and_12_out, and_13_out, not_1_out;

  not not_1 (not_1_out, Cn);
  and and_1 (and_1_out, nG0, not_1_out);
  and and_2 (and_2_out, nG0, nP0);
  nor nor_1 (Cn_x, and_2_out, and_1_out);
  and and_3 (and_3_out, nG0, nP0, nG1);
  and and_4 (and_4_out, nG1, nP1);
  nor nor_2 (Cn_y, and_4_out, and_3_out, and_5_out);
  and and_5 (and_5_out, nG0, nG1, not_1_out);
  and and_6 (and_6_out, nG2, nP2);
  and and_7 (and_7_out, nG1, nP1, nG2);
  nor nor_3 (Cn_z, and_6_out, and_7_out, and_8_out, and_10_out);
  and and_8 (and_8_out, nG0, nP0, nG1, nG2);
  and and_9 (and_9_out, nG3, nP3);
  and and_10 (and_10_out, nG0, nG1, nG2, not_1_out);
  and and_11 (and_11_out, nG2, nP2, nG3);
  or or_1 (nG, and_9_out, and_11_out, and_13_out, and_12_out);
  and and_12 (and_12_out, nG0, nG1, nG2, nG3);
  and and_13 (and_13_out, nG1, nP1, nG2, nG3);
  or or_2 (nP, nP0, nP1, nP2, nP3);
endmodule

module _377 (
  input  D,
  input  D_2,
  input  D_3,
  input  D_4,
  input  D_5,
  input  D_6,
  input  D_7,
  input  D_8,
  input  CLK,
  input  nG,
  output Q,
  output Q_2,
  output Q_3,
  output Q_4,
  output Q_5,
  output Q_6,
  output Q_7,
  output Q_8
);

  wire and_1_out, and_2_out;

  and and_1 (and_1_out, CLK, ~and_2_out);  // AND_Gate
  and and_2 (and_2_out, ~and_1_out, ~nG);  // AND_Gate
  D_Flip_Flop d_ff_1 (.clk(CLK), .D(D), .Q(Q), .en(and_2_out));  // open: Qn, preset, reset
  D_Flip_Flop d_ff_2 (.clk(CLK), .D(D_2), .Q(Q_2), .en(and_2_out));  // open: Qn, preset, reset
  D_Flip_Flop d_ff_3 (.clk(CLK), .D(D_3), .Q(Q_3), .en(and_2_out));  // open: Qn, preset, reset
  D_Flip_Flop d_ff_4 (.clk(CLK), .D(D_4), .Q(Q_4), .en(and_2_out));  // open: Qn, preset, reset
  D_Flip_Flop d_ff_5 (.clk(CLK), .D(D_5), .Q(Q_5), .en(and_2_out));  // open: Qn, preset, reset
  D_Flip_Flop d_ff_6 (.clk(CLK), .D(D_6), .Q(Q_6), .en(and_2_out));  // open: Qn, preset, reset
  D_Flip_Flop d_ff_7 (.clk(CLK), .D(D_7), .Q(Q_7), .en(and_2_out));  // open: Qn, preset, reset
  D_Flip_Flop d_ff_8 (.clk(CLK), .D(D_8), .Q(Q_8), .en(and_2_out));  // open: Qn, preset, reset
endmodule

module _641 (
  input  A,
  input  A_2,
  input  A_3,
  input  A_4,
  input  A_5,
  input  A_6,
  input  A_7,
  input  A_8,
  input  nG,
  input  A_B,
  input  B,
  input  B_2,
  input  B_3,
  input  B_4,
  input  B_5,
  input  B_6,
  input  B_7,
  input  B_8,
  output A_9,
  output A_10,
  output A_11,
  output A_12,
  output A_13,
  output A_14,
  output A_15,
  output A_16,
  output B_9,
  output B_10,
  output B_11,
  output B_12,
  output B_13,
  output B_14,
  output B_15,
  output B_16
);

  wire and_1_out, and_2_out;

  and and_1 (and_1_out, A_B, ~nG);  // AND_Gate
  nand nand_1 (A_9, ~B, and_2_out);  // NAND_Gate
  nand nand_2 (B_9, and_1_out, ~A);  // NAND_Gate
  and and_2 (and_2_out, ~A_B, ~nG);  // AND_Gate
  nand nand_3 (A_10, ~B_2, and_2_out);  // NAND_Gate
  nand nand_4 (B_11, and_1_out, ~A_3);  // NAND_Gate
  nand nand_5 (B_10, and_1_out, ~A_2);  // NAND_Gate
  nand nand_6 (A_11, ~B_3, and_2_out);  // NAND_Gate
  nand nand_7 (B_12, and_1_out, ~A_4);  // NAND_Gate
  nand nand_8 (A_12, ~B_4, and_2_out);  // NAND_Gate
  nand nand_9 (A_13, ~B_5, and_2_out);  // NAND_Gate
  nand nand_10 (B_13, and_1_out, ~A_5);  // NAND_Gate
  nand nand_11 (A_14, ~B_6, and_2_out);  // NAND_Gate
  nand nand_12 (B_15, and_1_out, ~A_7);  // NAND_Gate
  nand nand_13 (B_14, and_1_out, ~A_6);  // NAND_Gate
  nand nand_14 (A_15, ~B_7, and_2_out);  // NAND_Gate
  nand nand_15 (B_16, and_1_out, ~A_8);  // NAND_Gate
  nand nand_16 (A_16, ~B_8, and_2_out);  // NAND_Gate

  // Notes on the sheet:
  //   nand_1 drives only 0 and floats otherwise
  //   nand_2 drives only 0 and floats otherwise
  //   nand_3 drives only 0 and floats otherwise
  //   nand_4 drives only 0 and floats otherwise
  //   nand_5 drives only 0 and floats otherwise
  //   nand_6 drives only 0 and floats otherwise
  //   nand_7 drives only 0 and floats otherwise
  //   nand_8 drives only 0 and floats otherwise
  //   nand_9 drives only 0 and floats otherwise
  //   nand_10 drives only 0 and floats otherwise
  //   nand_11 drives only 0 and floats otherwise
  //   nand_12 drives only 0 and floats otherwise
  //   nand_13 drives only 0 and floats otherwise
  //   nand_14 drives only 0 and floats otherwise
  //   nand_15 drives only 0 and floats otherwise
  //   nand_16 drives only 0 and floats otherwise
endmodule

module _62256 (
  input  D,
  input  D_2,
  input  D_3,
  input  D_4,
  input  D_5,
  input  D_6,
  input  D_7,
  input  D_8,
  input  CLK,
  input  nCS,
  input  nWE,
  input  nOE,
  input  A,
  input  A_2,
  input  A_3,
  input  A_4,
  input  A_5,
  input  A_6,
  input  A_7,
  input  A_8,
  input  A_9,
  input  A_10,
  input  A_11,
  input  A_12,
  input  A_13,
  input  A_14,
  input  A_15,
  output D_9,
  output D_10,
  output D_11,
  output D_12,
  output D_13,
  output D_14,
  output D_15,
  output D_16
);

  wire and_1_out, and_2_out, not_1_out;
  wire [7:0] ram_1_data;

  and and_1 (and_1_out, ~nCS, ~nWE);  // AND_Gate
  and and_2 (and_2_out, ~nCS, ~nOE, nWE);  // AND_Gate
  RAM #(.addrWidth(15)) ram_1 (
    .addr({A_15, A_14, A_13, A_12, A_11, A_10, A_9, A_8, A_7, A_6, A_5, A_4, A_3, A_2, A}),
    .data(ram_1_data), .clk(CLK), .ld(not_1_out), .clr(1'b0));  // open: sel
  not not_1 (not_1_out, and_1_out);
  assign ram_1_data = and_1_out ? {D_8, D_7, D_6, D_5, D_4, D_3, D_2, D} : 8'bz;  // Controlled_Buffer controlled_buffer_1
  assign {D_16, D_15, D_14, D_13, D_12, D_11, D_10, D_9} = and_2_out ? ram_1_data : 8'bz;  // Controlled_Buffer controlled_buffer_2
endmodule
