// Logisim project clock.circ as structural Verilog: 1 circuit, main circuit main
module main (
  input  in_1,
  output out_2
);

  wire button_1_out, button_2_out, clock_1_out, nand_1_out, nand_2_out, nand_3_out, nand_4_out, nand_5_out,
       nand_7_out, nor_1_out, nor_2_out, not_1_out, not_2_out, not_3_out, not_4_out;

  Button button_1 (.out(button_1_out));
  Button button_2 (.out(button_2_out));
  nor nor_1 (nor_1_out, out_2, not_1_out);
  not not_1 (not_1_out, button_1_out);
  nor nor_2 (nor_2_out, out_2, not_2_out);
  not not_2 (not_2_out, button_2_out);
  not not_3 (not_3_out, nor_1_out);
  not not_4 (not_4_out, nor_2_out);
  Clock clock_1 (.out(clock_1_out));
  nand nand_1 (nand_1_out, not_3_out, nand_2_out);
  nand nand_2 (nand_2_out, nand_1_out, not_4_out, not_4_out);
  nand nand_3 (nand_3_out, not_4_out, nand_4_out);
  nand nand_4 (nand_4_out, nand_3_out, not_3_out, not_3_out);
  nand nand_5 (nand_5_out, in_1, nand_2_out);
  nand nand_6 (out_2, nand_5_out, nand_7_out);
  nand nand_7 (nand_7_out, clock_1_out, nand_4_out);
endmodule
